// Logisim project ALU.circ as structural Verilog: 7 circuits, main circuit main
module main (
);

  wire [7:0] register_1_out_5, register_2_out_5;

  register register_1 (.out_5(register_1_out_5));  // open: CLK, R_W, ENABLE, INPUT
  register register_2 (.out_5(register_2_out_5));  // open: CLK, R_W, ENABLE, INPUT

  // Notes on the sheet:
  //   L Register
  //   R Register
endmodule

module register (
  input  CLK,
  input  R_W,
  input  ENABLE,
  input  [7:0] INPUT,
  output [7:0] out_5
);

  wire and_1_out, and_2_out, and_3_out, and_4_out, and_5_out, and_6_out, and_7_out, and_8_out, and_9_out,
       and_10_out, not_1_out, not_2_out, not_3_out, not_4_out, not_5_out, not_6_out, not_7_out, not_8_out,
       not_9_out, s_r_ff_1_q, s_r_ff_2_q, s_r_ff_3_q, s_r_ff_4_q, s_r_ff_5_q, s_r_ff_6_q, s_r_ff_7_q,
       s_r_ff_8_q;

  and and_1 (and_1_out, CLK, ENABLE);
  and and_2 (and_2_out, CLK, R_W, ENABLE);
  and and_3 (and_3_out, INPUT[0], CLK, R_W);
  not not_1 (not_1_out, and_3_out);
  and and_4 (and_4_out, INPUT[1], CLK, R_W);
  not not_2 (not_2_out, and_4_out);
  and and_5 (and_5_out, INPUT[2], CLK, R_W);
  not not_3 (not_3_out, and_5_out);
  and and_6 (and_6_out, INPUT[3], CLK, R_W);
  not not_4 (not_4_out, and_6_out);
  and and_7 (and_7_out, INPUT[4], CLK, R_W);
  not not_5 (not_5_out, and_7_out);
  and and_8 (and_8_out, INPUT[5], CLK, R_W);
  not not_6 (not_6_out, and_8_out);
  and and_9 (and_9_out, INPUT[6], CLK, R_W);
  not not_7 (not_7_out, and_9_out);
  and and_10 (and_10_out, INPUT[7], CLK, R_W);
  not not_8 (not_8_out, and_10_out);
  not not_9 (not_9_out, R_W);
  S_R_Flip_Flop #(.trigger("high")) s_r_ff_1 (
    .S(and_3_out), .clk(and_2_out), .R(not_1_out), .Q(s_r_ff_1_q));  // open: Qn, preset, reset, en
  S_R_Flip_Flop #(.trigger("high")) s_r_ff_2 (
    .S(and_4_out), .clk(and_2_out), .R(not_2_out), .Q(s_r_ff_2_q));  // open: Qn, preset, reset, en
  S_R_Flip_Flop #(.trigger("high")) s_r_ff_3 (
    .S(and_5_out), .clk(and_2_out), .R(not_3_out), .Q(s_r_ff_3_q));  // open: Qn, preset, reset, en
  S_R_Flip_Flop #(.trigger("high")) s_r_ff_4 (
    .S(and_6_out), .clk(and_2_out), .R(not_4_out), .Q(s_r_ff_4_q));  // open: Qn, preset, reset, en
  S_R_Flip_Flop #(.trigger("high")) s_r_ff_5 (
    .S(and_7_out), .clk(and_2_out), .R(not_5_out), .Q(s_r_ff_5_q));  // open: Qn, preset, reset, en
  S_R_Flip_Flop #(.trigger("high")) s_r_ff_6 (
    .S(and_8_out), .clk(and_2_out), .R(not_6_out), .Q(s_r_ff_6_q));  // open: Qn, preset, reset, en
  S_R_Flip_Flop #(.trigger("high")) s_r_ff_7 (
    .S(and_9_out), .clk(and_2_out), .R(not_7_out), .Q(s_r_ff_7_q));  // open: Qn, preset, reset, en
  S_R_Flip_Flop #(.trigger("high")) s_r_ff_8 (
    .S(and_10_out), .clk(and_2_out), .R(not_8_out), .Q(s_r_ff_8_q));  // open: Qn, preset, reset, en
  and and_11 (out_5[0], s_r_ff_1_q, and_1_out, not_9_out);
  and and_12 (out_5[1], s_r_ff_2_q, and_1_out, not_9_out);
  and and_13 (out_5[2], s_r_ff_3_q, and_1_out, not_9_out);
  and and_14 (out_5[3], s_r_ff_4_q, and_1_out, not_9_out);
  and and_15 (out_5[4], s_r_ff_5_q, and_1_out, not_9_out);
  and and_16 (out_5[5], s_r_ff_6_q, and_1_out, not_9_out);
  and and_17 (out_5[6], s_r_ff_7_q, and_1_out, not_9_out);
  and and_18 (out_5[7], s_r_ff_8_q, and_1_out, not_9_out);
endmodule

module ALU (
  input  in_1,
  input  in_2,
  input  [7:0] in_3,
  input  [7:0] in_4,
  input  in_5,
  output Overflow,
  output Zero,
  output Negative,
  output [7:0] out_9
);

  wire and_17_out, and_18_out, and_19_out, and_20_out, and_21_out, and_22_out, and_23_out, and_24_out,
       and_25_out, and_26_out, and_27_out, and_28_out, and_29_out, and_30_out, and_31_out, and_32_out,
       full_adder_1_out_4, full_adder_1_out_5, full_adder_2_out_4, full_adder_2_out_5, full_adder_3_out_4,
       full_adder_3_out_5, full_adder_4_out_4, full_adder_4_out_5, full_adder_5_out_4, full_adder_5_out_5,
       full_adder_6_out_4, full_adder_6_out_5, full_adder_7_out_5, half_adder_1_out_3, half_adder_1_out_4,
       not_1_out, not_2_out, not_3_out, not_4_out, not_5_out, not_6_out, not_7_out, not_8_out, undriven,
       undriven_2, undriven_3, undriven_4, undriven_5, undriven_6, undriven_7, undriven_8;
  wire [7:0] alu2c_1_out_3;

  // AND_Gate and_1 has open pins: in0=in_3[0], in1=in_5, out=open
  // AND_Gate and_2 has open pins: in0=in_3[1], in1=in_5, out=open
  // AND_Gate and_3 has open pins: in0=in_3[2], in1=in_5, out=open
  // AND_Gate and_4 has open pins: in0=in_3[3], in1=in_5, out=open
  // AND_Gate and_5 has open pins: in0=in_3[4], in1=in_5, out=open
  // AND_Gate and_6 has open pins: in0=in_3[5], in1=in_5, out=open
  // AND_Gate and_7 has open pins: in0=in_3[6], in1=in_5, out=open
  // AND_Gate and_8 has open pins: in0=in_3[7], in1=in_5, out=open
  // AND_Gate and_9 has open pins: in0=in_4[0], in1=in_5, out=open
  // AND_Gate and_10 has open pins: in0=in_4[1], in1=in_5, out=open
  // AND_Gate and_11 has open pins: in0=in_4[2], in1=in_5, out=open
  // AND_Gate and_12 has open pins: in0=in_4[3], in1=in_5, out=open
  // AND_Gate and_13 has open pins: in0=in_4[4], in1=in_5, out=open
  // AND_Gate and_14 has open pins: in0=in_4[5], in1=in_5, out=open
  // AND_Gate and_15 has open pins: in0=in_4[6], in1=in_5, out=open
  // AND_Gate and_16 has open pins: in0=in_4[7], in1=in_5, out=open
  ALU2C alu2c_1 (.in_1(in_1), .in_2(in_4), .out_3(alu2c_1_out_3));
  and and_17 (and_17_out, in_3[0], in_2);
  and and_18 (and_18_out, in_3[1], in_2);
  and and_19 (and_19_out, in_3[2], in_2);
  and and_20 (and_20_out, in_3[3], in_2);
  and and_21 (and_21_out, in_3[4], in_2);
  and and_22 (and_22_out, in_3[5], in_2);
  and and_23 (and_23_out, in_3[6], in_2);
  and and_24 (and_24_out, in_3[7], in_2);
  and and_25 (and_25_out, alu2c_1_out_3[0], in_2);
  and and_26 (and_26_out, alu2c_1_out_3[1], in_2);
  and and_27 (and_27_out, alu2c_1_out_3[2], in_2);
  and and_28 (and_28_out, alu2c_1_out_3[3], in_2);
  and and_29 (and_29_out, alu2c_1_out_3[4], in_2);
  and and_30 (and_30_out, alu2c_1_out_3[5], in_2);
  and and_31 (and_31_out, alu2c_1_out_3[6], in_2);
  and and_32 (and_32_out, alu2c_1_out_3[7], in_2);
  half_adder half_adder_1 (
    .in_1(and_17_out), .in_2(and_25_out), .out_3(half_adder_1_out_3), .out_4(half_adder_1_out_4));
  full_adder full_adder_1 (
    .in_2(and_18_out), .in_3(and_26_out), .out_4(full_adder_1_out_4), .in_1(half_adder_1_out_4),
    .out_5(full_adder_1_out_5));
  full_adder full_adder_2 (
    .in_2(and_19_out), .in_3(and_27_out), .out_4(full_adder_2_out_4), .in_1(full_adder_1_out_5),
    .out_5(full_adder_2_out_5));
  full_adder full_adder_3 (
    .in_2(and_20_out), .in_3(and_28_out), .out_4(full_adder_3_out_4), .in_1(full_adder_2_out_5),
    .out_5(full_adder_3_out_5));
  full_adder full_adder_4 (
    .in_2(and_21_out), .in_3(and_29_out), .out_4(full_adder_4_out_4), .in_1(full_adder_3_out_5),
    .out_5(full_adder_4_out_5));
  full_adder full_adder_5 (
    .in_2(and_22_out), .in_3(and_30_out), .out_4(full_adder_5_out_4), .in_1(full_adder_4_out_5),
    .out_5(full_adder_5_out_5));
  full_adder full_adder_6 (
    .in_2(and_23_out), .in_3(and_31_out), .out_4(full_adder_6_out_4), .in_1(full_adder_5_out_5),
    .out_5(full_adder_6_out_5));
  full_adder full_adder_7 (
    .in_2(and_24_out), .in_3(and_32_out), .out_4(Negative), .in_1(full_adder_6_out_5),
    .out_5(full_adder_7_out_5));
  xor xor_1 (Overflow, full_adder_6_out_5, full_adder_7_out_5);
  not not_1 (not_1_out, Negative);
  not not_2 (not_2_out, full_adder_4_out_4);
  not not_3 (not_3_out, full_adder_5_out_4);
  not not_4 (not_4_out, full_adder_3_out_4);
  not not_5 (not_5_out, full_adder_6_out_4);
  and and_33 (Zero, not_1_out, not_5_out, not_3_out, not_2_out, not_4_out, not_7_out, not_6_out, not_8_out);
  not not_6 (not_6_out, full_adder_1_out_4);
  not not_7 (not_7_out, full_adder_2_out_4);
  not not_8 (not_8_out, half_adder_1_out_3);
  or or_1 (out_9[0], half_adder_1_out_3, undriven);
  or or_2 (out_9[1], full_adder_1_out_4, undriven_2);
  or or_3 (out_9[2], full_adder_2_out_4, undriven_3);
  or or_4 (out_9[3], full_adder_3_out_4, undriven_4);
  or or_5 (out_9[4], full_adder_4_out_4, undriven_5);
  or or_6 (out_9[5], full_adder_5_out_4, undriven_6);
  or or_7 (out_9[6], full_adder_6_out_4, undriven_7);
  or or_8 (out_9[7], Negative, undriven_8);

  // Notes on the sheet:
  //   R
  //   L
  //   SUB Section OPCODE required
  //   MULT SECTION OPCODE
  //   1 = SUB ON 0 = SUB OFF
  //   1= MULT ON 0= MULT OFF
  //   ADD Section OPCODE required
  //   1 = ADD ON 0 = ADD OFF
endmodule

module full_adder (
  input  in_1,
  input  in_2,
  input  in_3,
  output out_4,
  output out_5
);

  wire and_1_out, and_2_out, xor_1_out;

  xor xor_1 (xor_1_out, in_2, in_3);
  and and_1 (and_1_out, in_1, xor_1_out);
  or or_1 (out_5, and_1_out, and_2_out);
  and and_2 (and_2_out, in_2, in_3);
  xor xor_2 (out_4, in_1, xor_1_out);
endmodule

module half_adder (
  input  in_1,
  input  in_2,
  output out_3,
  output out_4
);

  xor xor_1 (out_3, in_1, in_2);
  and and_1 (out_4, in_1, in_2);
endmodule

module ALU2C (
  input  in_1,
  input  [7:0] in_2,
  output [7:0] out_3
);

  wire and_1_out, and_2_out, and_3_out, and_4_out, and_5_out, and_6_out, and_7_out, and_8_out, and_9_out,
       and_10_out, and_11_out, and_12_out, and_13_out, and_14_out, and_15_out, and_16_out,
       full_adder_1_out_5, full_adder_2_out_5, full_adder_3_out_5, full_adder_4_out_5, full_adder_5_out_5,
       full_adder_6_out_5, half_adder_1_out_4, not_1_out, not_2_out, not_3_out, not_4_out, not_5_out,
       not_6_out, not_7_out, not_8_out, not_9_out, not_10_out, not_11_out, not_12_out, not_13_out,
       not_14_out, not_15_out, not_16_out, or_1_out, or_2_out, or_3_out, or_4_out, or_5_out, or_6_out,
       or_7_out, or_8_out;

  not not_1 (not_1_out, in_1);
  not not_2 (not_2_out, in_2[0]);
  not not_3 (not_3_out, in_1);
  not not_4 (not_4_out, in_2[1]);
  not not_5 (not_5_out, in_1);
  not not_6 (not_6_out, in_2[2]);
  not not_7 (not_7_out, in_1);
  not not_8 (not_8_out, in_2[3]);
  not not_9 (not_9_out, in_1);
  not not_10 (not_10_out, in_2[4]);
  not not_11 (not_11_out, in_1);
  not not_12 (not_12_out, in_2[5]);
  not not_13 (not_13_out, in_1);
  not not_14 (not_14_out, in_2[6]);
  not not_15 (not_15_out, in_1);
  not not_16 (not_16_out, in_2[7]);
  and and_1 (and_1_out, not_1_out, in_2[0]);
  or or_1 (or_1_out, and_1_out, and_2_out);
  and and_2 (and_2_out, in_1, not_2_out);
  and and_3 (and_3_out, not_3_out, in_2[1]);
  or or_2 (or_2_out, and_3_out, and_4_out);
  and and_4 (and_4_out, in_1, not_4_out);
  and and_5 (and_5_out, not_5_out, in_2[2]);
  or or_3 (or_3_out, and_5_out, and_6_out);
  and and_6 (and_6_out, in_1, not_6_out);
  and and_7 (and_7_out, not_7_out, in_2[3]);
  or or_4 (or_4_out, and_7_out, and_8_out);
  and and_8 (and_8_out, in_1, not_8_out);
  and and_9 (and_9_out, not_9_out, in_2[4]);
  or or_5 (or_5_out, and_9_out, and_10_out);
  and and_10 (and_10_out, in_1, not_10_out);
  and and_11 (and_11_out, not_11_out, in_2[5]);
  or or_6 (or_6_out, and_11_out, and_12_out);
  and and_12 (and_12_out, in_1, not_12_out);
  and and_13 (and_13_out, not_13_out, in_2[6]);
  or or_7 (or_7_out, and_13_out, and_14_out);
  and and_14 (and_14_out, in_1, not_14_out);
  and and_15 (and_15_out, not_15_out, in_2[7]);
  or or_8 (or_8_out, and_15_out, and_16_out);
  and and_16 (and_16_out, in_1, not_16_out);
  half_adder half_adder_1 (.in_1(or_1_out), .in_2(in_1), .out_3(out_3[0]), .out_4(half_adder_1_out_4));
  full_adder full_adder_1 (
    .in_2(or_2_out), .in_3(1'b0), .out_4(out_3[1]), .in_1(half_adder_1_out_4), .out_5(full_adder_1_out_5));
  full_adder full_adder_2 (
    .in_2(or_3_out), .in_3(1'b0), .out_4(out_3[2]), .in_1(full_adder_1_out_5), .out_5(full_adder_2_out_5));
  full_adder full_adder_3 (
    .in_2(or_4_out), .in_3(1'b0), .out_4(out_3[3]), .in_1(full_adder_2_out_5), .out_5(full_adder_3_out_5));
  full_adder full_adder_4 (
    .in_2(or_5_out), .in_3(1'b0), .out_4(out_3[4]), .in_1(full_adder_3_out_5), .out_5(full_adder_4_out_5));
  full_adder full_adder_5 (
    .in_2(or_6_out), .in_3(1'b0), .out_4(out_3[5]), .in_1(full_adder_4_out_5), .out_5(full_adder_5_out_5));
  full_adder full_adder_6 (
    .in_2(or_7_out), .in_3(1'b0), .out_4(out_3[6]), .in_1(full_adder_5_out_5), .out_5(full_adder_6_out_5));
  full_adder full_adder_7 (.in_2(or_8_out), .in_3(1'b0), .out_4(out_3[7]), .in_1(full_adder_6_out_5));  // open: out_5
endmodule

module _16bitadder (
  input  [15:0] in_1,
  output [15:0] out_2
);

  wire full_adder_1_out_5, full_adder_2_out_5, full_adder_3_out_5, full_adder_4_out_5, full_adder_5_out_5,
       full_adder_6_out_5, full_adder_7_out_5, full_adder_8_out_5, full_adder_9_out_5, full_adder_10_out_5,
       full_adder_11_out_5, full_adder_12_out_5, full_adder_13_out_5, full_adder_14_out_5, half_adder_1_out_4;

  half_adder half_adder_1 (.in_1(in_1[0]), .in_2(1'b0), .out_3(out_2[0]), .out_4(half_adder_1_out_4));
  full_adder full_adder_1 (
    .in_2(in_1[1]), .in_3(1'b0), .out_4(out_2[1]), .in_1(half_adder_1_out_4), .out_5(full_adder_1_out_5));
  full_adder full_adder_2 (
    .in_2(in_1[2]), .in_3(1'b0), .out_4(out_2[2]), .in_1(full_adder_1_out_5), .out_5(full_adder_2_out_5));
  full_adder full_adder_3 (
    .in_2(in_1[3]), .in_3(1'b0), .out_4(out_2[3]), .in_1(full_adder_2_out_5), .out_5(full_adder_3_out_5));
  full_adder full_adder_4 (
    .in_2(in_1[4]), .in_3(1'b0), .out_4(out_2[4]), .in_1(full_adder_3_out_5), .out_5(full_adder_4_out_5));
  full_adder full_adder_5 (
    .in_2(in_1[5]), .in_3(1'b0), .out_4(out_2[5]), .in_1(full_adder_4_out_5), .out_5(full_adder_5_out_5));
  full_adder full_adder_6 (
    .in_2(in_1[6]), .in_3(1'b0), .out_4(out_2[6]), .in_1(full_adder_5_out_5), .out_5(full_adder_6_out_5));
  full_adder full_adder_7 (
    .in_2(in_1[7]), .in_3(1'b0), .out_4(out_2[7]), .in_1(full_adder_6_out_5), .out_5(full_adder_7_out_5));
  full_adder full_adder_8 (
    .in_2(in_1[8]), .in_3(1'b0), .out_4(out_2[8]), .in_1(full_adder_7_out_5), .out_5(full_adder_8_out_5));
  full_adder full_adder_9 (
    .in_2(in_1[9]), .in_3(1'b0), .out_4(out_2[9]), .in_1(full_adder_8_out_5), .out_5(full_adder_9_out_5));
  full_adder full_adder_10 (
    .in_2(in_1[10]), .in_3(1'b0), .out_4(out_2[10]), .in_1(full_adder_9_out_5), .out_5(full_adder_10_out_5));
  full_adder full_adder_11 (
    .in_2(in_1[11]), .in_3(1'b0), .out_4(out_2[11]), .in_1(full_adder_10_out_5), .out_5(full_adder_11_out_5));
  full_adder full_adder_12 (
    .in_2(in_1[12]), .in_3(1'b0), .out_4(out_2[12]), .in_1(full_adder_11_out_5), .out_5(full_adder_12_out_5));
  full_adder full_adder_13 (
    .in_2(in_1[13]), .in_3(1'b0), .out_4(out_2[13]), .in_1(full_adder_12_out_5), .out_5(full_adder_13_out_5));
  full_adder full_adder_14 (
    .in_2(in_1[14]), .in_3(1'b0), .out_4(out_2[14]), .in_1(full_adder_13_out_5), .out_5(full_adder_14_out_5));
  full_adder full_adder_15 (
    .in_2(in_1[15]), .in_3(1'b0), .out_4(out_2[15]), .in_1(full_adder_14_out_5));  // open: out_5
endmodule
