// Logisim project CPU.circ as structural Verilog: 25 circuits, main circuit main
module main (
  input  in_1,
  input  in_2,
  input  in_3,
  input  in_4,
  input  Mode,
  input  [7:0] INSTR,
  input  From_INSTR,
  input  From_PC,
  input  [7:0] From_DR,
  input  in_10,
  input  From_MBR,
  input  in_12,
  input  in_13,
  input  in_14,
  input  in_15,
  input  in_16,
  input  in_17,
  input  in_18,
  input  in_19,
  input  in_20,
  input  in_21,
  input  in_22,
  input  in_23,
  input  in_24,
  input  in_25,
  input  in_26,
  output [7:0] AR,
  output [7:0] To_DR,
  output [7:0] CPU_BUS
);

  wire clock_1_out, not_1_out;
  wire [2:0] alu_1_overflow, statusregister_1_out_5;
  wire [7:0] alu_1_out_9, demultiplexer_1_out1, incrementer_1_out_2, n2_combinator_1_out_5,
       n2_combinator_2_out_5, n5_combinator_2_out_11, pcregister_1_out_7, register_2_out_5, register_3_out_5,
       register_4_out_5, register_5_out_5, register_6_out_5, register_7_out_5, undriven;

  _2_Combinator u_2_combinator_1 (
    .in_2(From_DR), .in_4(undriven), .out_5(n2_combinator_1_out_5), .in_1(not_1_out), .in_3(in_10));
  not not_1 (not_1_out, in_10);
  register register_1 (.CLK(clock_1_out), .R_W(in_3), .ENABLE(in_4), .INPUT(pcregister_1_out_7), .out_5(AR));
  register register_2 (
    .CLK(clock_1_out), .R_W(in_2), .ENABLE(in_1), .INPUT(n2_combinator_1_out_5), .out_5(register_2_out_5));
  Clock clock_1 (.out(clock_1_out));
  register register_3 (
    .CLK(clock_1_out), .R_W(in_18), .ENABLE(in_19), .INPUT(n5_combinator_2_out_11), .out_5(register_3_out_5));
  register register_4 (
    .CLK(clock_1_out), .R_W(in_23), .ENABLE(in_24), .INPUT(n5_combinator_2_out_11), .out_5(register_4_out_5));
  Demultiplexer #(.width(8), .disabled(0), .enable("false")) demultiplexer_1 (
    .out0(To_DR), .out1(demultiplexer_1_out1), .in(register_2_out_5), .sel(From_MBR));
  _5_combinator u_5_combinator_1 (
    .in_2({{5{1'b0}}, statusregister_1_out_5}), .in_4(register_6_out_5), .in_6(register_3_out_5),
    .in_8(register_4_out_5), .in_10(undriven), .out_11(CPU_BUS), .in_1(in_17), .in_3(in_25), .in_5(in_19),
    .in_7(in_24), .in_9(in_10));
  Incrementer incrementer_1 (.in_1(AR), .out_2(incrementer_1_out_2));
  StatusRegister statusregister_1 (
    .CLK(clock_1_out), .R_W(in_16), .ENABLE(in_17), .INPUT(alu_1_overflow), .out_5(statusregister_1_out_5));
  _2_Combinator u_2_combinator_2 (
    .in_2(INSTR), .in_4(incrementer_1_out_2), .out_5(n2_combinator_2_out_5), .in_1(From_INSTR), .in_3(From_PC));
  register register_5 (
    .CLK(clock_1_out), .R_W(in_13), .ENABLE(in_12), .INPUT(n5_combinator_2_out_11), .out_5(register_5_out_5));
  register register_6 (.CLK(clock_1_out), .R_W(in_26), .ENABLE(in_25), .INPUT(alu_1_out_9), .out_5(register_6_out_5));
  PCregister pcregister_1 (
    .CLK(clock_1_out), .in_4(n2_combinator_2_out_5), .out_7(pcregister_1_out_7));  // open: R_W, ENABLE, in_5, in_6
  register register_7 (
    .CLK(clock_1_out), .R_W(in_15), .ENABLE(in_14), .INPUT(n5_combinator_2_out_11), .out_5(register_7_out_5));
  ALU alu_1 (
    .in_3(register_7_out_5), .in_4(register_5_out_5), .in_5(in_22), .in_2(in_20), .in_1(in_21),
    .Overflow(alu_1_overflow[0]), .Zero(alu_1_overflow[1]), .Negative(alu_1_overflow[2]), .out_9(alu_1_out_9));
  _5_combinator u_5_combinator_2 (
    .in_2(CPU_BUS), .in_4(CPU_BUS), .in_6(CPU_BUS), .in_8(CPU_BUS), .in_10(demultiplexer_1_out1),
    .out_11(n5_combinator_2_out_11), .in_1(in_12), .in_3(in_14), .in_5(in_19), .in_7(in_24), .in_9(From_MBR));

  // Notes on the sheet:
  //   PC Increment through MAR Value
  //   MAR
  //   MBR
  //   D0
  //   D1
  //   DR
  //   To MBR
  //   beq bnq flag
  //   INSTR
  //   L Register
  //   A out
  //   R Register
endmodule

module RAM_project (
  input  ADDR,
  input  in_2,
  input  in_3,
  input  in_4,
  input  R_W,
  input  DATA,
  input  in_7,
  input  in_8,
  input  in_9,
  input  in_10,
  input  in_11,
  input  in_12,
  input  in_13
);

  wire and_1_out, and_2_out, and_3_out, and_4_out, and_5_out, and_6_out, and_7_out, and_8_out, and_9_out,
       and_10_out, and_11_out, and_12_out, and_13_out, and_14_out, and_15_out, and_16_out, and_17_out,
       CLOCK_out, n4to16_1_addr0, n4to16_1_addr1, n4to16_1_addr2, n4to16_1_addr3, n4to16_1_addr4,
       n4to16_1_addr5, n4to16_1_addr6, n4to16_1_addr7, n4to16_1_addr8, n4to16_1_addr9, n4to16_1_addr10,
       n4to16_1_addr11, n4to16_1_addr12, n4to16_1_addr13, n4to16_1_addr14, n4to16_1_addr15, not_1_out,
       not_2_out, not_3_out, not_4_out, not_5_out, not_6_out, not_7_out, not_8_out, not_9_out, not_10_out,
       not_11_out, not_12_out, not_13_out, not_14_out, or_1_out, or_2_out, or_3_out, or_4_out, or_5_out,
       or_6_out, or_7_out, or_8_out, s_r_ff_1_q, s_r_ff_2_q, s_r_ff_3_q, s_r_ff_4_q, s_r_ff_5_q, s_r_ff_6_q,
       s_r_ff_7_q, s_r_ff_8_q, s_r_ff_9_q, s_r_ff_10_q, s_r_ff_11_q, s_r_ff_12_q, s_r_ff_13_q;
  wire [7:0] and_25_out, byte_1_outputbits, byte_2_outputbits, byte_3_outputbits, byte_4_outputbits,
       byte_5_outputbits, byte_6_outputbits, byte_7_outputbits, byte_8_outputbits, byte_9_outputbits,
       byte_10_outputbits, byte_11_outputbits, byte_12_outputbits, byte_13_outputbits, byte_14_outputbits,
       byte_15_outputbits, byte_16_outputbits, combinator_1_out_17;

  Clock CLOCK (.out(CLOCK_out));
  not not_1 (not_1_out, R_W);
  and and_1 (and_1_out, DATA, R_W);
  and and_2 (and_2_out, in_7, R_W);
  and and_3 (and_3_out, in_8, R_W);
  and and_4 (and_4_out, in_9, R_W);
  and and_5 (and_5_out, in_10, R_W);
  and and_6 (and_6_out, in_11, R_W);
  and and_7 (and_7_out, in_12, R_W);
  and and_8 (and_8_out, in_13, R_W);
  and and_9 (and_9_out, combinator_1_out_17[0], not_1_out);
  and and_10 (and_10_out, combinator_1_out_17[1], not_1_out);
  and and_11 (and_11_out, combinator_1_out_17[3], not_1_out);
  and and_12 (and_12_out, combinator_1_out_17[2], not_1_out);
  S_R_Flip_Flop s_r_ff_1 (.Q(s_r_ff_1_q), .preset(in_4), .reset(not_2_out));  // open: S, clk, R, Qn, en
  not not_2 (not_2_out, in_4);
  S_R_Flip_Flop s_r_ff_2 (.Q(s_r_ff_2_q), .preset(in_3), .reset(not_3_out));  // open: S, clk, R, Qn, en
  not not_3 (not_3_out, in_3);
  S_R_Flip_Flop s_r_ff_3 (.Q(s_r_ff_3_q), .preset(in_2), .reset(not_4_out));  // open: S, clk, R, Qn, en
  not not_4 (not_4_out, in_2);
  S_R_Flip_Flop s_r_ff_4 (.Q(s_r_ff_4_q), .preset(ADDR), .reset(not_5_out));  // open: S, clk, R, Qn, en
  not not_5 (not_5_out, ADDR);
  S_R_Flip_Flop s_r_ff_5 (.Q(s_r_ff_5_q), .preset(R_W), .reset(not_6_out));  // open: S, clk, R, Qn, en
  not not_6 (not_6_out, R_W);
  and and_13 (and_13_out, combinator_1_out_17[5], not_1_out);
  and and_14 (and_14_out, combinator_1_out_17[4], not_1_out);
  and and_15 (and_15_out, combinator_1_out_17[6], not_1_out);
  and and_16 (and_16_out, combinator_1_out_17[7], not_1_out);
  or or_1 (or_1_out, and_1_out, and_9_out);
  or or_2 (or_2_out, and_2_out, and_10_out);
  or or_3 (or_3_out, and_3_out, and_12_out);
  or or_4 (or_4_out, and_4_out, and_11_out);
  or or_5 (or_5_out, and_5_out, and_14_out);
  or or_6 (or_6_out, and_6_out, and_13_out);
  or or_7 (or_7_out, and_7_out, and_15_out);
  or or_8 (or_8_out, and_8_out, and_16_out);
  _4to16 u_4to16_1 (
    .value(CLOCK_out), .bit3(s_r_ff_4_q), .bit2(s_r_ff_3_q), .bit1(s_r_ff_2_q), .bit0(s_r_ff_1_q),
    .ADDR0(n4to16_1_addr0), .ADDR1(n4to16_1_addr1), .ADDR2(n4to16_1_addr2), .ADDR3(n4to16_1_addr3),
    .ADDR4(n4to16_1_addr4), .ADDR5(n4to16_1_addr5), .ADDR6(n4to16_1_addr6), .ADDR7(n4to16_1_addr7),
    .ADDR8(n4to16_1_addr8), .ADDR9(n4to16_1_addr9), .ADDR10(n4to16_1_addr10), .ADDR11(n4to16_1_addr11),
    .ADDR12(n4to16_1_addr12), .ADDR13(n4to16_1_addr13), .ADDR14(n4to16_1_addr14), .ADDR15(n4to16_1_addr15));
  and and_17 (and_17_out, CLOCK_out, s_r_ff_5_q);
  S_R_Flip_Flop s_r_ff_6 (.S(or_1_out), .clk(CLOCK_out), .R(not_7_out), .Q(s_r_ff_6_q));  // open: Qn, preset, reset, en
  not not_7 (not_7_out, or_1_out);
  S_R_Flip_Flop s_r_ff_7 (.S(or_2_out), .clk(CLOCK_out), .R(not_8_out), .Q(s_r_ff_7_q));  // open: Qn, preset, reset, en
  not not_8 (not_8_out, or_2_out);
  S_R_Flip_Flop s_r_ff_8 (.S(or_3_out), .clk(CLOCK_out), .R(not_9_out), .Q(s_r_ff_8_q));  // open: Qn, preset, reset, en
  not not_9 (not_9_out, or_3_out);
  S_R_Flip_Flop s_r_ff_9 (
    .S(or_4_out), .clk(CLOCK_out), .R(not_10_out), .Q(s_r_ff_9_q));  // open: Qn, preset, reset, en
  not not_10 (not_10_out, or_4_out);
  S_R_Flip_Flop s_r_ff_10 (
    .S(or_5_out), .clk(CLOCK_out), .R(not_11_out), .Q(s_r_ff_10_q));  // open: Qn, preset, reset, en
  not not_11 (not_11_out, or_5_out);
  S_R_Flip_Flop s_r_ff_11 (
    .S(or_6_out), .clk(CLOCK_out), .R(not_12_out), .Q(s_r_ff_11_q));  // open: Qn, preset, reset, en
  not not_12 (not_12_out, or_6_out);
  S_R_Flip_Flop s_r_ff_12 (
    .S(or_7_out), .clk(CLOCK_out), .R(not_13_out), .Q(s_r_ff_12_q));  // open: Qn, preset, reset, en
  not not_13 (not_13_out, or_7_out);
  S_R_Flip_Flop s_r_ff_13 (
    .S(or_8_out), .clk(CLOCK_out), .R(not_14_out), .Q(s_r_ff_13_q));  // open: Qn, preset, reset, en
  not not_14 (not_14_out, or_8_out);
  and and_18 (and_25_out[6], s_r_ff_7_q, and_17_out);
  and and_19 (and_25_out[7], s_r_ff_6_q, and_17_out);
  and and_20 (and_25_out[4], s_r_ff_9_q, and_17_out);
  and and_21 (and_25_out[3], s_r_ff_10_q, and_17_out);
  and and_22 (and_25_out[5], s_r_ff_8_q, and_17_out);
  and and_23 (and_25_out[1], s_r_ff_12_q, and_17_out);
  and and_24 (and_25_out[2], s_r_ff_11_q, and_17_out);
  and and_25 (and_25_out[0], s_r_ff_13_q, and_17_out);
  \byte  byte_1 (
    .InputBits(and_25_out), .Outputbits(byte_1_outputbits), .CLOCK(CLOCK_out), .RW(and_17_out),
    .EN(n4to16_1_addr15));
  \byte  byte_2 (
    .InputBits(and_25_out), .Outputbits(byte_2_outputbits), .CLOCK(CLOCK_out), .RW(and_17_out),
    .EN(n4to16_1_addr14));
  \byte  byte_3 (
    .InputBits(and_25_out), .Outputbits(byte_3_outputbits), .CLOCK(CLOCK_out), .RW(and_17_out),
    .EN(n4to16_1_addr13));
  \byte  byte_4 (
    .InputBits(and_25_out), .Outputbits(byte_4_outputbits), .CLOCK(CLOCK_out), .RW(and_17_out),
    .EN(n4to16_1_addr12));
  \byte  byte_5 (
    .InputBits(and_25_out), .Outputbits(byte_5_outputbits), .CLOCK(CLOCK_out), .RW(and_17_out),
    .EN(n4to16_1_addr11));
  \byte  byte_6 (
    .InputBits(and_25_out), .Outputbits(byte_6_outputbits), .CLOCK(CLOCK_out), .RW(and_17_out),
    .EN(n4to16_1_addr10));
  \byte  byte_7 (
    .InputBits(and_25_out), .Outputbits(byte_7_outputbits), .CLOCK(CLOCK_out), .RW(and_17_out),
    .EN(n4to16_1_addr9));
  \byte  byte_8 (
    .InputBits(and_25_out), .Outputbits(byte_8_outputbits), .CLOCK(CLOCK_out), .RW(and_17_out),
    .EN(n4to16_1_addr8));
  \byte  byte_9 (
    .InputBits(and_25_out), .Outputbits(byte_9_outputbits), .CLOCK(CLOCK_out), .RW(and_17_out),
    .EN(n4to16_1_addr7));
  \byte  byte_10 (
    .InputBits(and_25_out), .Outputbits(byte_10_outputbits), .CLOCK(CLOCK_out), .RW(and_17_out),
    .EN(n4to16_1_addr6));
  \byte  byte_11 (
    .InputBits(and_25_out), .Outputbits(byte_11_outputbits), .CLOCK(CLOCK_out), .RW(and_17_out),
    .EN(n4to16_1_addr5));
  \byte  byte_12 (
    .InputBits(and_25_out), .Outputbits(byte_12_outputbits), .CLOCK(CLOCK_out), .RW(and_17_out),
    .EN(n4to16_1_addr4));
  \byte  byte_13 (
    .InputBits(and_25_out), .Outputbits(byte_13_outputbits), .CLOCK(CLOCK_out), .RW(and_17_out),
    .EN(n4to16_1_addr3));
  \byte  byte_14 (
    .InputBits(and_25_out), .Outputbits(byte_14_outputbits), .CLOCK(CLOCK_out), .RW(and_17_out),
    .EN(n4to16_1_addr2));
  \byte  byte_15 (
    .InputBits(and_25_out), .Outputbits(byte_15_outputbits), .CLOCK(CLOCK_out), .RW(and_17_out),
    .EN(n4to16_1_addr1));
  \byte  byte_16 (
    .InputBits(and_25_out), .Outputbits(byte_16_outputbits), .CLOCK(CLOCK_out), .RW(and_17_out),
    .EN(n4to16_1_addr0));
  COMBINATOR combinator_1 (
    .in_1(byte_16_outputbits), .in_2(byte_15_outputbits), .in_3(byte_14_outputbits),
    .in_4(byte_13_outputbits), .in_5(byte_12_outputbits), .in_6(byte_11_outputbits),
    .in_7(byte_10_outputbits), .in_8(byte_9_outputbits), .in_9(byte_8_outputbits), .in_10(byte_7_outputbits),
    .in_11(byte_6_outputbits), .in_12(byte_5_outputbits), .in_13(byte_4_outputbits),
    .in_14(byte_3_outputbits), .in_15(byte_2_outputbits), .in_16(byte_1_outputbits),
    .out_17(combinator_1_out_17));
endmodule

module _4to16 (
  input  value,
  input  bit3,
  input  bit2,
  input  bit1,
  input  bit0,
  output ADDR0,
  output ADDR1,
  output ADDR2,
  output ADDR3,
  output ADDR4,
  output ADDR5,
  output ADDR6,
  output ADDR7,
  output ADDR8,
  output ADDR9,
  output ADDR10,
  output ADDR11,
  output ADDR12,
  output ADDR13,
  output ADDR14,
  output ADDR15
);

  wire not_1_out, not_2_out, not_3_out, not_4_out, not_5_out, not_6_out, not_7_out, not_8_out, not_9_out,
       not_10_out, not_11_out, not_12_out, not_13_out, not_14_out, not_15_out, not_16_out, not_17_out,
       not_18_out, not_19_out, not_20_out, not_21_out, not_22_out, not_23_out, not_24_out, not_25_out,
       not_26_out, not_27_out, not_28_out, not_29_out, not_30_out, not_31_out, not_32_out;

  not not_1 (not_1_out, bit1);
  not not_2 (not_2_out, bit0);
  not not_3 (not_3_out, bit2);
  not not_4 (not_4_out, bit3);
  not not_5 (not_5_out, bit1);
  not not_6 (not_6_out, bit2);
  and u_addr0 (ADDR0, not_2_out, not_1_out, not_3_out, not_4_out, value);
  and u_addr1 (ADDR1, bit0, not_5_out, not_6_out, not_8_out, value);
  not not_7 (not_7_out, bit2);
  not not_8 (not_8_out, bit3);
  not not_9 (not_9_out, bit0);
  not not_10 (not_10_out, bit3);
  and u_addr2 (ADDR2, not_9_out, bit1, not_7_out, not_10_out, value);
  not not_11 (not_11_out, bit3);
  not not_12 (not_12_out, bit2);
  and u_addr3 (ADDR3, bit0, bit1, not_12_out, not_11_out, value);
  not not_13 (not_13_out, bit1);
  not not_14 (not_14_out, bit3);
  not not_15 (not_15_out, bit0);
  and u_addr4 (ADDR4, not_15_out, not_13_out, bit2, not_14_out, value);
  not not_16 (not_16_out, bit1);
  not not_17 (not_17_out, bit3);
  and u_addr5 (ADDR5, bit0, not_16_out, bit2, not_17_out, value);
  not not_18 (not_18_out, bit0);
  not not_19 (not_19_out, bit3);
  and u_addr6 (ADDR6, not_18_out, bit1, bit2, not_19_out, value);
  not not_20 (not_20_out, bit1);
  not not_21 (not_21_out, bit3);
  not not_22 (not_22_out, bit0);
  and u_addr7 (ADDR7, bit0, bit1, bit2, not_21_out, value);
  not not_23 (not_23_out, bit2);
  not not_24 (not_24_out, bit2);
  not not_25 (not_25_out, bit1);
  and u_addr9 (ADDR9, bit0, not_25_out, not_24_out, bit3, value);
  and u_addr8 (ADDR8, not_22_out, not_20_out, not_23_out, bit3, value);
  not not_26 (not_26_out, bit2);
  not not_27 (not_27_out, bit0);
  and add10 (ADDR10, not_27_out, bit1, not_26_out, bit3, value);
  not not_28 (not_28_out, bit2);
  and u_addr11 (ADDR11, bit0, bit1, not_28_out, bit3, value);
  not not_29 (not_29_out, bit0);
  not not_30 (not_30_out, bit1);
  and u_addr12 (ADDR12, not_29_out, not_30_out, bit2, bit3, value);
  not not_31 (not_31_out, bit1);
  and u_addr13 (ADDR13, bit0, not_31_out, bit2, bit3, value);
  not not_32 (not_32_out, bit0);
  and u_addr14 (ADDR14, not_32_out, bit1, bit2, bit3, value);
  and u_addr15 (ADDR15, bit0, bit1, bit2, bit3, value);

  // Notes on the sheet:
  //   2
endmodule

module COMBINATOR (
  input  [7:0] in_1,
  input  [7:0] in_2,
  input  [7:0] in_3,
  input  [7:0] in_4,
  input  [7:0] in_5,
  input  [7:0] in_6,
  input  [7:0] in_7,
  input  [7:0] in_8,
  input  [7:0] in_9,
  input  [7:0] in_10,
  input  [7:0] in_11,
  input  [7:0] in_12,
  input  [7:0] in_13,
  input  [7:0] in_14,
  input  [7:0] in_15,
  input  [7:0] in_16,
  output [7:0] out_17
);

  or or_1 (out_17[0], in_16[0], in_15[0], in_14[0], in_13[0], in_12[0], in_11[0], in_10[0], in_9[0], in_8[0], in_7[0], in_6[0], in_5[0], in_4[0], in_3[0], in_2[0], in_1[0]);
  or or_2 (out_17[1], in_16[1], in_15[1], in_14[1], in_13[1], in_12[1], in_11[1], in_10[1], in_9[1], in_8[1], in_7[1], in_6[1], in_5[1], in_4[1], in_3[1], in_2[1], in_1[1]);
  or or_3 (out_17[2], in_16[2], in_15[2], in_14[2], in_13[2], in_12[2], in_11[2], in_10[2], in_9[2], in_8[2], in_7[2], in_6[2], in_5[2], in_4[2], in_3[2], in_2[2], in_1[2]);
  or or_4 (out_17[3], in_16[3], in_15[3], in_14[3], in_13[3], in_12[3], in_11[3], in_10[3], in_9[3], in_8[3], in_7[3], in_6[3], in_5[3], in_4[3], in_3[3], in_2[3], in_1[3]);
  or or_5 (out_17[4], in_16[4], in_15[4], in_14[4], in_13[4], in_12[4], in_11[4], in_10[4], in_9[4], in_8[4], in_7[4], in_6[4], in_5[4], in_4[4], in_3[4], in_2[4], in_1[4]);
  or or_6 (out_17[5], in_16[5], in_15[5], in_14[5], in_13[5], in_12[5], in_11[5], in_10[5], in_9[5], in_8[5], in_7[5], in_6[5], in_5[5], in_4[5], in_3[5], in_2[5], in_1[5]);
  or or_7 (out_17[6], in_16[6], in_15[6], in_14[6], in_13[6], in_12[6], in_11[6], in_10[6], in_9[6], in_8[6], in_7[6], in_6[6], in_5[6], in_4[6], in_3[6], in_2[6], in_1[6]);
  or or_8 (out_17[7], in_16[7], in_15[7], in_14[7], in_13[7], in_12[7], in_11[7], in_10[7], in_9[7], in_8[7], in_7[7], in_6[7], in_5[7], in_4[7], in_3[7], in_2[7], in_1[7]);
endmodule

module \byte  (
  input  CLOCK,
  input  RW,
  input  EN,
  input  [7:0] InputBits,
  output [7:0] Outputbits
);

  wire and_1_out, and_2_out, and_3_out, and_4_out, and_5_out, and_6_out, and_7_out, and_8_out, and_9_out,
       and_10_out, not_1_out, not_2_out, not_3_out, not_4_out, not_5_out, not_6_out, not_7_out, not_8_out,
       not_9_out, s_r_ff_1_q, s_r_ff_2_q, s_r_ff_3_q, s_r_ff_4_q, s_r_ff_5_q, s_r_ff_6_q, s_r_ff_7_q,
       s_r_ff_8_q;

  and and_1 (and_1_out, CLOCK, RW, EN, InputBits[0]);
  and and_2 (and_2_out, CLOCK, RW, EN, InputBits[1]);
  and and_3 (and_3_out, CLOCK, RW, EN, InputBits[2]);
  and and_4 (and_4_out, CLOCK, RW, EN, InputBits[3]);
  and and_5 (and_5_out, CLOCK, RW, EN, InputBits[4]);
  and and_6 (and_6_out, CLOCK, EN, InputBits[5]);
  and and_7 (and_7_out, CLOCK, RW, EN, InputBits[6]);
  and and_8 (and_8_out, CLOCK, RW, EN, InputBits[7]);
  and and_9 (and_9_out, EN, RW, CLOCK);
  not not_1 (not_1_out, RW);
  and and_10 (and_10_out, EN, not_1_out, CLOCK);
  S_R_Flip_Flop #(.trigger("high")) s_r_ff_1 (
    .S(and_1_out), .clk(and_9_out), .R(not_2_out), .Q(s_r_ff_1_q));  // open: Qn, preset, reset, en
  not not_2 (not_2_out, and_1_out);
  S_R_Flip_Flop #(.trigger("high")) s_r_ff_2 (
    .S(and_2_out), .clk(and_9_out), .R(not_3_out), .Q(s_r_ff_2_q));  // open: Qn, preset, reset, en
  not not_3 (not_3_out, and_2_out);
  S_R_Flip_Flop #(.trigger("high")) s_r_ff_3 (
    .S(and_3_out), .clk(and_9_out), .R(not_4_out), .Q(s_r_ff_3_q));  // open: Qn, preset, reset, en
  not not_4 (not_4_out, and_3_out);
  S_R_Flip_Flop #(.trigger("high")) s_r_ff_4 (
    .S(and_4_out), .clk(and_9_out), .R(not_5_out), .Q(s_r_ff_4_q));  // open: Qn, preset, reset, en
  not not_5 (not_5_out, and_4_out);
  S_R_Flip_Flop #(.trigger("high")) s_r_ff_5 (
    .S(and_5_out), .clk(and_9_out), .R(not_6_out), .Q(s_r_ff_5_q));  // open: Qn, preset, reset, en
  not not_6 (not_6_out, and_5_out);
  S_R_Flip_Flop #(.trigger("high")) s_r_ff_6 (
    .S(and_6_out), .clk(and_9_out), .R(not_7_out), .Q(s_r_ff_6_q));  // open: Qn, preset, reset, en
  not not_7 (not_7_out, and_6_out);
  S_R_Flip_Flop #(.trigger("high")) s_r_ff_7 (
    .S(and_7_out), .clk(and_9_out), .R(not_8_out), .Q(s_r_ff_7_q));  // open: Qn, preset, reset, en
  not not_8 (not_8_out, and_7_out);
  S_R_Flip_Flop #(.trigger("high")) s_r_ff_8 (
    .S(and_8_out), .clk(and_9_out), .R(not_9_out), .Q(s_r_ff_8_q));  // open: Qn, preset, reset, en
  not not_9 (not_9_out, and_8_out);
  and and_11 (Outputbits[0], s_r_ff_1_q, and_10_out);
  and and_12 (Outputbits[1], s_r_ff_2_q, and_10_out);
  and and_13 (Outputbits[2], s_r_ff_3_q, and_10_out);
  and and_14 (Outputbits[3], s_r_ff_4_q, and_10_out);
  and and_15 (Outputbits[4], s_r_ff_5_q, and_10_out);
  and and_16 (Outputbits[5], s_r_ff_6_q, and_10_out);
  and and_17 (Outputbits[6], s_r_ff_7_q, and_10_out);
  and and_18 (Outputbits[7], s_r_ff_8_q, and_10_out);
endmodule

module CPU_project (
  input  [7:0] in_1
);

  wire display_1_a, display_1_b, display_1_c, display_1_d, display_1_e, display_1_f, display_1_g,
       display_2_a, display_2_b, display_2_c, display_2_d, display_2_e, display_2_f, display_2_g,
       display_3_a, display_3_b, display_3_c, display_3_d, display_3_e, display_3_f, display_3_g;
  wire [3:0] makingbdc_1_out_2, makingbdc_1_out_3, makingbdc_1_out_4;

  display display_1 (
    .d(display_1_d), .e(display_1_e), .g(display_1_g), .b(display_1_b), .a(display_1_a), .c(display_1_c),
    .f(display_1_f), .in_1(makingbdc_1_out_2));
  display display_2 (
    .d(display_2_d), .e(display_2_e), .g(display_2_g), .b(display_2_b), .a(display_2_a), .c(display_2_c),
    .f(display_2_f), .in_1(makingbdc_1_out_3));
  makingBDC makingbdc_1 (.in_1(in_1), .out_2(makingbdc_1_out_2), .out_3(makingbdc_1_out_3), .out_4(makingbdc_1_out_4));
  display display_3 (
    .d(display_3_d), .e(display_3_e), .g(display_3_g), .b(display_3_b), .a(display_3_a), .c(display_3_c),
    .f(display_3_f), .in_1(makingbdc_1_out_4));
  RAM_project RAM ();  // open: DATA, in_7, in_8, in_9, in_10, in_11, in_12, in_13, R_W, ADDR, in_2, in_3, in_4
  _7_Segment_Display u_7_segment_display_1 (
    .g(display_3_d), .f(display_3_b), .a(display_3_a), .b(display_3_c), .e(display_3_e), .d(display_3_g),
    .c(display_3_f));  // open: dp
  _7_Segment_Display u_7_segment_display_2 (
    .g(display_2_d), .f(display_2_b), .a(display_2_a), .b(display_2_c), .e(display_2_e), .d(display_2_g),
    .c(display_2_f));  // open: dp
  _7_Segment_Display u_7_segment_display_3 (
    .g(display_1_d), .f(display_1_b), .a(display_1_a), .b(display_1_c), .e(display_1_e), .d(display_1_g),
    .c(display_1_f));  // open: dp
endmodule

module display (
  input  [3:0] in_1,
  output a,
  output b,
  output c,
  output d,
  output f,
  output e,
  output g
);

  wire _0_out, _1_out, _2_out, _3_out, _4_out, _5_out, _6_out, _7_out, _9_out, _10_plus_out, a_out,
       and_1_out, and_2_out, b_out, c_out, d_out, e_out, f_out, g_out, not_1_out, not_2_out, not_3_out,
       not_4_out, not_5_out, not_6_out, not_7_out, not_8_out, not_9_out, not_10_out, not_11_out, not_12_out,
       not_13_out, not_14_out, not_15_out, not_16_out, not_17_out, not_18_out, not_19_out, not_20_out,
       not_21_out, not_22_out;

  not not_1 (not_1_out, in_1[1]);
  not not_2 (not_2_out, in_1[2]);
  not not_3 (not_3_out, in_1[3]);
  not not_4 (not_4_out, in_1[0]);
  not not_5 (not_5_out, in_1[1]);
  not not_6 (not_6_out, in_1[3]);
  not not_7 (not_7_out, in_1[0]);
  not not_8 (not_8_out, in_1[2]);
  not not_9 (not_9_out, in_1[3]);
  not not_10 (not_10_out, in_1[2]);
  not not_11 (not_11_out, in_1[3]);
  not not_12 (not_12_out, in_1[3]);
  not not_13 (not_13_out, in_1[1]);
  not not_14 (not_14_out, in_1[3]);
  not not_15 (not_15_out, in_1[0]);
  not not_16 (not_16_out, in_1[3]);
  not not_17 (not_17_out, in_1[0]);
  not not_18 (not_18_out, in_1[1]);
  not not_19 (not_19_out, in_1[2]);
  not not_20 (not_20_out, in_1[3]);
  not not_21 (not_21_out, in_1[1]);
  not not_22 (not_22_out, in_1[2]);
  and and_1 (and_1_out, in_1[1], in_1[3]);
  and and_2 (and_2_out, in_1[2], in_1[3]);
  and _1 (_1_out, in_1[0], not_1_out, not_2_out, not_3_out);
  and _4 (_4_out, not_4_out, not_5_out, in_1[2], not_6_out);
  and _2 (_2_out, not_7_out, in_1[1], not_8_out, not_9_out);
  and _3 (_3_out, in_1[0], in_1[1], not_10_out, not_11_out);
  and _7 (_7_out, in_1[0], in_1[1], in_1[2], not_12_out);
  and _5 (_5_out, in_1[0], not_13_out, in_1[2], not_14_out);
  and _6 (_6_out, not_15_out, in_1[1], in_1[2], not_16_out);
  and _0 (_0_out, not_17_out, not_18_out, not_19_out, not_20_out);
  and _9 (_9_out, in_1[0], not_21_out, not_22_out, in_1[3]);
  or _10_plus (_10_plus_out, and_1_out, and_2_out);
  or u_a (a_out, _1_out, _4_out);
  or u_b (b_out, _1_out, _2_out, _3_out, _7_out);
  or u_c (c_out, _5_out, _10_plus_out, _6_out);
  or u_d (d_out, _7_out, _1_out, _0_out);
  or u_e (e_out, _1_out, _3_out, _4_out, _5_out, _7_out, _9_out);
  or u_f (f_out, _2_out, _10_plus_out);
  or u_g (g_out, _7_out, _4_out, _1_out);
  not not_23 (a, a_out);
  not not_24 (b, b_out);
  not not_25 (c, c_out);
  not not_26 (d, d_out);
  not not_27 (e, e_out);
  not not_28 (f, f_out);
  not not_29 (g, g_out);
endmodule

module decoder8to3_4s (
  input  in_1,
  input  in_2,
  input  in_3,
  input  in_4,
  output out_5,
  output out_6,
  output out_7,
  output out_8
);

  wire _0_out, _1_out, _2_out, _3_out, _4_out, _5_out, _6_out, _7_out, _8_out, _9_out, and_1_out, and_2_out,
       and_3_out, and_4_out, and_5_out, and_6_out, and_7_out, and_8_out, and_9_out, and_10_out, and_11_out,
       and_12_out, and_13_out, and_14_out, and_15_out, and_16_out, and_17_out, and_18_out, and_19_out,
       and_20_out, and_21_out, and_22_out, and_23_out, and_24_out, and_25_out, and_26_out, and_27_out,
       and_28_out, and_29_out, and_30_out, and_31_out, and_32_out, and_33_out, and_34_out, and_35_out,
       and_36_out, and_37_out, and_38_out, and_39_out, and_40_out, not_1_out, not_2_out, not_3_out,
       not_4_out, not_5_out, not_6_out, not_7_out, not_8_out, not_9_out, not_10_out, not_11_out, not_12_out,
       not_13_out, not_14_out, not_15_out, not_16_out, not_17_out, not_18_out, not_19_out, not_20_out,
       not_21_out, not_22_out, not_23_out, not_24_out, not_25_out, not_26_out, not_27_out, not_28_out,
       not_29_out, not_30_out, not_31_out, not_32_out, not_33_out, not_34_out, not_35_out, not_36_out,
       not_37_out, not_38_out, not_39_out, not_40_out, not_41_out, not_42_out, not_43_out, not_44_out,
       not_45_out, not_46_out, not_47_out, not_48_out, not_49_out, not_50_out;

  not not_1 (not_1_out, in_1);
  not not_2 (not_2_out, in_2);
  not not_3 (not_3_out, in_3);
  not not_4 (not_4_out, in_4);
  not not_5 (not_5_out, in_2);
  not not_6 (not_6_out, in_3);
  not not_7 (not_7_out, in_4);
  not not_8 (not_8_out, in_1);
  not not_9 (not_9_out, in_3);
  not not_10 (not_10_out, in_4);
  not not_11 (not_11_out, in_3);
  not not_12 (not_12_out, in_4);
  not not_13 (not_13_out, in_1);
  not not_14 (not_14_out, in_2);
  not not_15 (not_15_out, in_4);
  not not_16 (not_16_out, in_2);
  not not_17 (not_17_out, in_4);
  not not_18 (not_18_out, in_1);
  not not_19 (not_19_out, in_4);
  not not_20 (not_20_out, in_4);
  not not_21 (not_21_out, in_1);
  not not_22 (not_22_out, in_2);
  not not_23 (not_23_out, in_3);
  not not_24 (not_24_out, in_2);
  not not_25 (not_25_out, in_3);
  and _0 (_0_out, not_1_out, not_2_out, not_3_out, not_4_out);
  and _1 (_1_out, in_1, not_5_out, not_6_out, not_7_out);
  and _2 (_2_out, not_8_out, in_2, not_9_out, not_10_out);
  and _3 (_3_out, in_1, in_2, not_11_out, not_12_out);
  and _4 (_4_out, not_13_out, not_14_out, in_3, not_15_out);
  and _5 (_5_out, in_1, not_16_out, in_3, not_17_out);
  and _6 (_6_out, not_18_out, in_2, in_3, not_19_out);
  and _7 (_7_out, in_1, in_2, in_3, not_20_out);
  and _8 (_8_out, not_21_out, not_22_out, not_23_out, in_4);
  and _9 (_9_out, in_1, not_24_out, not_25_out, in_4);
  not not_26 (not_26_out, _0_out);
  not not_27 (not_27_out, _0_out);
  not not_28 (not_28_out, _0_out);
  not not_29 (not_29_out, _0_out);
  not not_30 (not_30_out, _1_out);
  not not_31 (not_31_out, _1_out);
  not not_32 (not_32_out, _1_out);
  not not_33 (not_33_out, _2_out);
  not not_34 (not_34_out, _2_out);
  not not_35 (not_35_out, _2_out);
  not not_36 (not_36_out, _3_out);
  not not_37 (not_37_out, _3_out);
  not not_38 (not_38_out, _4_out);
  not not_39 (not_39_out, _4_out);
  not not_40 (not_40_out, _4_out);
  not not_41 (not_41_out, _5_out);
  not not_42 (not_42_out, _5_out);
  not not_43 (not_43_out, _5_out);
  not not_44 (not_44_out, _6_out);
  not not_45 (not_45_out, _6_out);
  not not_46 (not_46_out, _7_out);
  not not_47 (not_47_out, _7_out);
  not not_48 (not_48_out, _8_out);
  not not_49 (not_49_out, _9_out);
  not not_50 (not_50_out, _9_out);
  and and_1 (and_1_out, not_26_out, _0_out);
  and and_2 (and_2_out, not_27_out, _0_out);
  and and_3 (and_3_out, not_28_out, _0_out);
  and and_4 (and_4_out, not_29_out, _0_out);
  and and_5 (and_5_out, _1_out, _1_out);
  and and_6 (and_6_out, not_30_out, _1_out);
  and and_7 (and_7_out, not_31_out, _1_out);
  and and_8 (and_8_out, not_32_out, _1_out);
  and and_9 (and_9_out, not_33_out, _2_out);
  and and_10 (and_10_out, _2_out, _2_out);
  and and_11 (and_11_out, not_34_out, _2_out);
  and and_12 (and_12_out, not_35_out, _2_out);
  and and_13 (and_13_out, _3_out, _3_out);
  and and_14 (and_14_out, _3_out, _3_out);
  and and_15 (and_15_out, not_36_out, _3_out);
  and and_16 (and_16_out, not_37_out, _3_out);
  and and_17 (and_17_out, not_38_out, _4_out);
  and and_18 (and_18_out, not_39_out, _4_out);
  and and_19 (and_19_out, _4_out, _4_out);
  and and_20 (and_20_out, not_40_out, _4_out);
  and and_21 (and_21_out, not_41_out, _5_out);
  and and_22 (and_22_out, not_42_out, _5_out);
  and and_23 (and_23_out, not_43_out, _5_out);
  and and_24 (and_24_out, _5_out, _5_out);
  and and_25 (and_25_out, _6_out, _6_out);
  and and_26 (and_26_out, not_44_out, _6_out);
  and and_27 (and_27_out, not_45_out, _6_out);
  and and_28 (and_28_out, _6_out, _6_out);
  and and_29 (and_29_out, not_46_out, _7_out);
  and and_30 (and_30_out, _7_out, _7_out);
  and and_31 (and_31_out, not_47_out, _7_out);
  and and_32 (and_32_out, _7_out, _7_out);
  and and_33 (and_33_out, _8_out, _8_out);
  and and_34 (and_34_out, _8_out, _8_out);
  and and_35 (and_35_out, not_48_out, _8_out);
  and and_36 (and_36_out, _8_out, _8_out);
  and and_37 (and_37_out, not_49_out, _9_out);
  and and_38 (and_38_out, not_50_out, _9_out);
  and and_39 (and_39_out, _9_out, _9_out);
  and and_40 (and_40_out, _9_out, _9_out);
  or or_1 (out_8, and_1_out, and_5_out, and_9_out, and_13_out, and_17_out, and_21_out, and_25_out, and_29_out, and_33_out, and_37_out);
  or or_2 (out_7, and_2_out, and_6_out, and_10_out, and_14_out, and_18_out, and_22_out, and_26_out, and_30_out, and_34_out, and_38_out);
  or or_3 (out_6, and_3_out, and_7_out, and_11_out, and_15_out, and_19_out, and_23_out, and_27_out, and_31_out, and_35_out, and_39_out);
  or or_4 (out_5, and_4_out, and_8_out, and_12_out, and_16_out, and_20_out, and_24_out, and_28_out, and_32_out, and_36_out, and_40_out);
endmodule

module makingBDC (
  input  [7:0] in_1,
  output [3:0] out_2,
  output [3:0] out_3,
  output [3:0] out_4
);

  wire decoder8to3_4s_1_out_5, decoder8to3_4s_1_out_6, decoder8to3_4s_1_out_7, decoder8to3_4s_1_out_8,
       decoder8to3_4s_2_out_6, decoder8to3_4s_2_out_7, decoder8to3_4s_2_out_8, decoder8to3_4s_4_out_5,
       decoder8to3_4s_4_out_6, decoder8to3_4s_4_out_7, decoder8to3_4s_4_out_8, decoder8to3_4s_5_out_5,
       decoder8to3_4s_5_out_6, decoder8to3_4s_5_out_7, decoder8to3_4s_5_out_8, decoder8to3_4s_6_out_5,
       decoder8to3_4s_6_out_6, decoder8to3_4s_6_out_7, decoder8to3_4s_6_out_8;

  decoder8to3_4s decoder8to3_4s_1 (
    .in_1(in_1[5]), .in_2(in_1[6]), .out_5(decoder8to3_4s_1_out_5), .in_3(in_1[7]),
    .out_6(decoder8to3_4s_1_out_6), .in_4(1'b0), .out_7(decoder8to3_4s_1_out_7),
    .out_8(decoder8to3_4s_1_out_8));
  decoder8to3_4s decoder8to3_4s_2 (
    .in_1(decoder8to3_4s_5_out_5), .in_2(decoder8to3_4s_4_out_5), .out_5(out_4[1]),
    .in_3(decoder8to3_4s_1_out_5), .out_6(decoder8to3_4s_2_out_6), .in_4(1'b0),
    .out_7(decoder8to3_4s_2_out_7), .out_8(decoder8to3_4s_2_out_8));
  decoder8to3_4s decoder8to3_4s_3 (
    .in_1(decoder8to3_4s_6_out_5), .in_2(decoder8to3_4s_2_out_8), .out_5(out_4[0]),
    .in_3(decoder8to3_4s_2_out_7), .out_6(out_3[3]), .in_4(decoder8to3_4s_2_out_6), .out_7(out_3[2]),
    .out_8(out_3[1]));
  decoder8to3_4s decoder8to3_4s_4 (
    .in_1(in_1[4]), .in_2(decoder8to3_4s_1_out_8), .out_5(decoder8to3_4s_4_out_5),
    .in_3(decoder8to3_4s_1_out_7), .out_6(decoder8to3_4s_4_out_6), .in_4(decoder8to3_4s_1_out_6),
    .out_7(decoder8to3_4s_4_out_7), .out_8(decoder8to3_4s_4_out_8));
  decoder8to3_4s decoder8to3_4s_5 (
    .in_1(in_1[3]), .in_2(decoder8to3_4s_4_out_8), .out_5(decoder8to3_4s_5_out_5),
    .in_3(decoder8to3_4s_4_out_7), .out_6(decoder8to3_4s_5_out_6), .in_4(decoder8to3_4s_4_out_6),
    .out_7(decoder8to3_4s_5_out_7), .out_8(decoder8to3_4s_5_out_8));
  decoder8to3_4s decoder8to3_4s_6 (
    .in_1(in_1[2]), .in_2(decoder8to3_4s_5_out_8), .out_5(decoder8to3_4s_6_out_5),
    .in_3(decoder8to3_4s_5_out_7), .out_6(decoder8to3_4s_6_out_6), .in_4(decoder8to3_4s_5_out_6),
    .out_7(decoder8to3_4s_6_out_7), .out_8(decoder8to3_4s_6_out_8));
  decoder8to3_4s decoder8to3_4s_7 (
    .in_1(in_1[1]), .in_2(decoder8to3_4s_6_out_8), .out_5(out_3[0]), .in_3(decoder8to3_4s_6_out_7),
    .out_6(out_2[3]), .in_4(decoder8to3_4s_6_out_6), .out_7(out_2[2]), .out_8(out_2[1]));

  assign out_2[0] = in_1[0];
  assign out_4[3:2] = 2'b00;
endmodule

module keypad_buffer (
  input  ENTER,
  input  [7:0] in_2,
  output [7:0] out_3
);

  D_Flip_Flop d_ff_1 (.clk(ENTER), .D(in_2[0]), .Q(out_3[0]));  // open: Qn, preset, en, reset
  D_Flip_Flop d_ff_2 (.clk(ENTER), .D(in_2[1]), .Q(out_3[1]));  // open: Qn, preset, en, reset
  D_Flip_Flop d_ff_3 (.clk(ENTER), .D(in_2[2]), .Q(out_3[2]));  // open: Qn, preset, en, reset
  D_Flip_Flop d_ff_4 (.clk(ENTER), .D(in_2[3]), .Q(out_3[3]));  // open: Qn, preset, en, reset
  D_Flip_Flop d_ff_5 (.clk(ENTER), .D(in_2[4]), .Q(out_3[4]));  // open: Qn, preset, en, reset
  D_Flip_Flop d_ff_6 (.clk(ENTER), .D(in_2[5]), .Q(out_3[5]));  // open: Qn, preset, en, reset
  D_Flip_Flop d_ff_7 (.clk(ENTER), .D(in_2[6]), .Q(out_3[6]));  // open: Qn, preset, en, reset
  D_Flip_Flop d_ff_8 (.clk(ENTER), .D(in_2[7]), .Q(out_3[7]));  // open: Qn, preset, en, reset
endmodule

module keypad_buttons_and_outputs (
  input  _0,
  input  _1,
  input  _2,
  input  _3,
  input  _4,
  input  _5,
  input  _6,
  input  _7,
  input  _8,
  input  _9,
  input  ENTER,
  output [7:0] out_12
);

  wire and_2_out, and_3_out, and_4_out, and_5_out, and_6_out, and_7_out, and_8_out, and_9_out, and_10_out;

  // AND_Gate and_1 has open pins: in0=_0, in1=1'b1, out=open
  and and_2 (and_2_out, _1, 1'b1);
  and and_3 (and_3_out, _2, 1'b1);
  and and_4 (and_4_out, _3, 1'b1);
  and and_5 (and_5_out, _4, 1'b1);
  and and_6 (and_6_out, _5, 1'b1);
  and and_7 (and_7_out, _6, 1'b1);
  and and_8 (and_8_out, _7, 1'b1);
  and and_9 (and_9_out, _8, 1'b1);
  and and_10 (and_10_out, _9, 1'b1);
  or or_1 (out_12[3], 1'b0, and_2_out, 1'b0, and_4_out, 1'b0, and_6_out, 1'b0, and_8_out, 1'b0, and_10_out);
  or or_2 (out_12[2], 1'b0, 1'b0, and_3_out, and_4_out, 1'b0, 1'b0, and_7_out, and_8_out, 1'b0, 1'b0);
  or or_3 (out_12[1], 1'b0, 1'b0, 1'b0, 1'b0, and_5_out, and_6_out, and_7_out, and_8_out, 1'b0, 1'b0);
  or or_4 (out_12[0], 1'b0, 1'b0, 1'b0, 1'b0, 1'b0, 1'b0, 1'b0, 1'b0, and_9_out, and_10_out);

  assign out_12[7:4] = 4'b0000;
endmodule

module register (
  input  CLK,
  input  R_W,
  input  ENABLE,
  input  [7:0] INPUT,
  output [7:0] out_5
);

  wire and_1_out, and_2_out, and_3_out, and_4_out, and_5_out, and_6_out, and_7_out, and_8_out, and_9_out,
       and_10_out, not_1_out, not_2_out, not_3_out, not_4_out, not_5_out, not_6_out, not_7_out, not_8_out,
       not_9_out, s_r_ff_1_q, s_r_ff_2_q, s_r_ff_3_q, s_r_ff_4_q, s_r_ff_5_q, s_r_ff_6_q, s_r_ff_7_q,
       s_r_ff_8_q;

  and and_1 (and_1_out, CLK, ENABLE);
  and and_2 (and_2_out, CLK, R_W, ENABLE);
  and and_3 (and_3_out, INPUT[0], CLK, R_W);
  not not_1 (not_1_out, and_3_out);
  and and_4 (and_4_out, INPUT[1], CLK, R_W);
  not not_2 (not_2_out, and_4_out);
  and and_5 (and_5_out, INPUT[2], CLK, R_W);
  not not_3 (not_3_out, and_5_out);
  and and_6 (and_6_out, INPUT[3], CLK, R_W);
  not not_4 (not_4_out, and_6_out);
  and and_7 (and_7_out, INPUT[4], CLK, R_W);
  not not_5 (not_5_out, and_7_out);
  and and_8 (and_8_out, INPUT[5], CLK, R_W);
  not not_6 (not_6_out, and_8_out);
  and and_9 (and_9_out, INPUT[6], CLK, R_W);
  not not_7 (not_7_out, and_9_out);
  and and_10 (and_10_out, INPUT[7], CLK, R_W);
  not not_8 (not_8_out, and_10_out);
  not not_9 (not_9_out, R_W);
  S_R_Flip_Flop #(.trigger("high")) s_r_ff_1 (
    .S(and_3_out), .clk(and_2_out), .R(not_1_out), .Q(s_r_ff_1_q));  // open: Qn, preset, reset, en
  S_R_Flip_Flop #(.trigger("high")) s_r_ff_2 (
    .S(and_4_out), .clk(and_2_out), .R(not_2_out), .Q(s_r_ff_2_q));  // open: Qn, preset, reset, en
  S_R_Flip_Flop #(.trigger("high")) s_r_ff_3 (
    .S(and_5_out), .clk(and_2_out), .R(not_3_out), .Q(s_r_ff_3_q));  // open: Qn, preset, reset, en
  S_R_Flip_Flop #(.trigger("high")) s_r_ff_4 (
    .S(and_6_out), .clk(and_2_out), .R(not_4_out), .Q(s_r_ff_4_q));  // open: Qn, preset, reset, en
  S_R_Flip_Flop #(.trigger("high")) s_r_ff_5 (
    .S(and_7_out), .clk(and_2_out), .R(not_5_out), .Q(s_r_ff_5_q));  // open: Qn, preset, reset, en
  S_R_Flip_Flop #(.trigger("high")) s_r_ff_6 (
    .S(and_8_out), .clk(and_2_out), .R(not_6_out), .Q(s_r_ff_6_q));  // open: Qn, preset, reset, en
  S_R_Flip_Flop #(.trigger("high")) s_r_ff_7 (
    .S(and_9_out), .clk(and_2_out), .R(not_7_out), .Q(s_r_ff_7_q));  // open: Qn, preset, reset, en
  S_R_Flip_Flop #(.trigger("high")) s_r_ff_8 (
    .S(and_10_out), .clk(and_2_out), .R(not_8_out), .Q(s_r_ff_8_q));  // open: Qn, preset, reset, en
  and and_11 (out_5[0], s_r_ff_1_q, and_1_out, not_9_out);
  and and_12 (out_5[1], s_r_ff_2_q, and_1_out, not_9_out);
  and and_13 (out_5[2], s_r_ff_3_q, and_1_out, not_9_out);
  and and_14 (out_5[3], s_r_ff_4_q, and_1_out, not_9_out);
  and and_15 (out_5[4], s_r_ff_5_q, and_1_out, not_9_out);
  and and_16 (out_5[5], s_r_ff_6_q, and_1_out, not_9_out);
  and and_17 (out_5[6], s_r_ff_7_q, and_1_out, not_9_out);
  and and_18 (out_5[7], s_r_ff_8_q, and_1_out, not_9_out);
endmodule

module ALU (
  input  in_1,
  input  in_2,
  input  [7:0] in_3,
  input  [7:0] in_4,
  input  in_5,
  output Overflow,
  output Zero,
  output Negative,
  output [7:0] out_9
);

  wire and_1_out, and_2_out, and_3_out, and_4_out, and_5_out, and_6_out, and_7_out, and_8_out, and_17_out,
       and_18_out, and_19_out, and_20_out, and_21_out, and_22_out, and_23_out, and_24_out, and_25_out,
       and_26_out, and_27_out, and_28_out, and_29_out, and_30_out, and_31_out, and_32_out,
       full_adder_1_out_4, full_adder_1_out_5, full_adder_2_out_4, full_adder_2_out_5, full_adder_3_out_4,
       full_adder_3_out_5, full_adder_4_out_4, full_adder_4_out_5, full_adder_5_out_4, full_adder_5_out_5,
       full_adder_6_out_4, full_adder_6_out_5, full_adder_7_out_4, full_adder_7_out_5, half_adder_1_out_3,
       half_adder_1_out_4, not_1_out, not_2_out, not_3_out, not_4_out, not_5_out, not_6_out, not_7_out,
       not_8_out, not_9_out, or_1_out, or_3_out, xor_1_out;
  wire [7:0] alu2c_1_out_3, and_9_out;
  wire [15:0] adder_1_out, adder_2_out, adder_3_out, adder_4_out, adder_5_out, adder_6_out, adder_7_out,
       adder_8_out, multhelper_1_out_3, multhelper_2_out_3, multhelper_3_out_3, multhelper_4_out_3,
       multhelper_5_out_3, multhelper_6_out_3, multhelper_7_out_3, multhelper_8_out_3, n16bitshift_1_out_2,
       n16bitshift_2_out_2, n16bitshift_3_out_2, n16bitshift_4_out_2, n16bitshift_5_out_2,
       n16bitshift_6_out_2, n16bitshift_7_out_2, n16bitshift_8_out_2, n16bitshift_9_out_2,
       n16bitshift_10_out_2, n16bitshift_11_out_2, n16bitshift_12_out_2, n16bitshift_13_out_2,
       n16bitshift_14_out_2, n16bitshift_15_out_2, n16bitshift_16_out_2, n16bitshift_17_out_2,
       n16bitshift_18_out_2, n16bitshift_19_out_2, n16bitshift_20_out_2, n16bitshift_21_out_2,
       n16bitshift_22_out_2, n16bitshift_23_out_2, n16bitshift_24_out_2, n16bitshift_25_out_2,
       n16bitshift_26_out_2, n16bitshift_27_out_2, n16bitshift_28_out_2;

  and and_1 (and_1_out, in_3[0], in_5);
  and and_2 (and_2_out, in_3[1], in_5);
  and and_3 (and_3_out, in_3[2], in_5);
  and and_4 (and_4_out, in_3[3], in_5);
  and and_5 (and_5_out, in_3[4], in_5);
  and and_6 (and_6_out, in_3[5], in_5);
  and and_7 (and_7_out, in_3[6], in_5);
  and and_8 (and_8_out, in_3[7], in_5);
  and and_9 (and_9_out[0], in_4[0], in_5);
  and and_10 (and_9_out[1], in_4[1], in_5);
  and and_11 (and_9_out[2], in_4[2], in_5);
  and and_12 (and_9_out[3], in_4[3], in_5);
  and and_13 (and_9_out[4], in_4[4], in_5);
  and and_14 (and_9_out[5], in_4[5], in_5);
  and and_15 (and_9_out[6], in_4[6], in_5);
  and and_16 (and_9_out[7], in_4[7], in_5);
  ALU2C alu2c_1 (.in_1(in_2), .in_2(in_4), .out_3(alu2c_1_out_3));
  or or_1 (or_1_out, in_1, in_2);
  multhelper multhelper_1 (.in_1({{8{1'b0}}, and_9_out}), .out_3(multhelper_1_out_3), .in_2(and_1_out));
  and and_17 (and_17_out, in_3[0], or_1_out);
  and and_18 (and_18_out, in_3[1], or_1_out);
  and and_19 (and_19_out, in_3[2], or_1_out);
  and and_20 (and_20_out, in_3[3], or_1_out);
  and and_21 (and_21_out, in_3[4], or_1_out);
  and and_22 (and_22_out, in_3[5], or_1_out);
  and and_23 (and_23_out, in_3[6], or_1_out);
  and and_24 (and_24_out, in_3[7], or_1_out);
  and and_25 (and_25_out, alu2c_1_out_3[0], or_1_out);
  and and_26 (and_26_out, alu2c_1_out_3[1], or_1_out);
  and and_27 (and_27_out, alu2c_1_out_3[2], or_1_out);
  and and_28 (and_28_out, alu2c_1_out_3[3], or_1_out);
  and and_29 (and_29_out, alu2c_1_out_3[4], or_1_out);
  and and_30 (and_30_out, alu2c_1_out_3[5], or_1_out);
  and and_31 (and_31_out, alu2c_1_out_3[6], or_1_out);
  and and_32 (and_32_out, alu2c_1_out_3[7], or_1_out);
  Adder #(.width(16)) adder_1 (.a(multhelper_1_out_3), .b({16{1'b0}}), .out(adder_1_out));  // open: cin, cout
  multhelper multhelper_2 (.in_1({{8{1'b0}}, and_9_out}), .out_3(multhelper_2_out_3), .in_2(and_2_out));
  _16bitshift u_16bitshift_1 (.in_1(multhelper_2_out_3), .out_2(n16bitshift_1_out_2));
  Adder #(.width(16)) adder_2 (.a(n16bitshift_1_out_2), .b(adder_1_out), .out(adder_2_out));  // open: cin, cout
  multhelper multhelper_3 (.in_1({{8{1'b0}}, and_9_out}), .out_3(multhelper_3_out_3), .in_2(and_3_out));
  _16bitshift u_16bitshift_2 (.in_1(multhelper_3_out_3), .out_2(n16bitshift_2_out_2));
  _16bitshift u_16bitshift_3 (.in_1(n16bitshift_2_out_2), .out_2(n16bitshift_3_out_2));
  Adder #(.width(16)) adder_3 (.a(n16bitshift_3_out_2), .b(adder_2_out), .out(adder_3_out));  // open: cin, cout
  multhelper multhelper_4 (.in_1({{8{1'b0}}, and_9_out}), .out_3(multhelper_4_out_3), .in_2(and_4_out));
  _16bitshift u_16bitshift_4 (.in_1(multhelper_4_out_3), .out_2(n16bitshift_4_out_2));
  _16bitshift u_16bitshift_5 (.in_1(n16bitshift_4_out_2), .out_2(n16bitshift_5_out_2));
  _16bitshift u_16bitshift_6 (.in_1(n16bitshift_5_out_2), .out_2(n16bitshift_6_out_2));
  Adder #(.width(16)) adder_4 (.a(n16bitshift_6_out_2), .b(adder_3_out), .out(adder_4_out));  // open: cin, cout
  half_adder half_adder_1 (
    .in_1(and_17_out), .in_2(and_25_out), .out_3(half_adder_1_out_3), .out_4(half_adder_1_out_4));
  full_adder full_adder_1 (
    .in_2(and_18_out), .in_3(and_26_out), .out_4(full_adder_1_out_4), .in_1(half_adder_1_out_4),
    .out_5(full_adder_1_out_5));
  full_adder full_adder_2 (
    .in_2(and_19_out), .in_3(and_27_out), .out_4(full_adder_2_out_4), .in_1(full_adder_1_out_5),
    .out_5(full_adder_2_out_5));
  full_adder full_adder_3 (
    .in_2(and_20_out), .in_3(and_28_out), .out_4(full_adder_3_out_4), .in_1(full_adder_2_out_5),
    .out_5(full_adder_3_out_5));
  full_adder full_adder_4 (
    .in_2(and_21_out), .in_3(and_29_out), .out_4(full_adder_4_out_4), .in_1(full_adder_3_out_5),
    .out_5(full_adder_4_out_5));
  full_adder full_adder_5 (
    .in_2(and_22_out), .in_3(and_30_out), .out_4(full_adder_5_out_4), .in_1(full_adder_4_out_5),
    .out_5(full_adder_5_out_5));
  full_adder full_adder_6 (
    .in_2(and_23_out), .in_3(and_31_out), .out_4(full_adder_6_out_4), .in_1(full_adder_5_out_5),
    .out_5(full_adder_6_out_5));
  full_adder full_adder_7 (
    .in_2(and_24_out), .in_3(and_32_out), .out_4(full_adder_7_out_4), .in_1(full_adder_6_out_5),
    .out_5(full_adder_7_out_5));
  multhelper multhelper_5 (.in_1({{8{1'b0}}, and_9_out}), .out_3(multhelper_5_out_3), .in_2(and_5_out));
  _16bitshift u_16bitshift_7 (.in_1(multhelper_5_out_3), .out_2(n16bitshift_7_out_2));
  _16bitshift u_16bitshift_8 (.in_1(n16bitshift_7_out_2), .out_2(n16bitshift_8_out_2));
  _16bitshift u_16bitshift_9 (.in_1(n16bitshift_8_out_2), .out_2(n16bitshift_9_out_2));
  _16bitshift u_16bitshift_10 (.in_1(n16bitshift_9_out_2), .out_2(n16bitshift_10_out_2));
  Adder #(.width(16)) adder_5 (.a(n16bitshift_10_out_2), .b(adder_4_out), .out(adder_5_out));  // open: cin, cout
  xor xor_1 (xor_1_out, full_adder_6_out_5, full_adder_7_out_5);
  multhelper multhelper_6 (.in_1({{8{1'b0}}, and_9_out}), .out_3(multhelper_6_out_3), .in_2(and_6_out));
  _16bitshift u_16bitshift_11 (.in_1(multhelper_6_out_3), .out_2(n16bitshift_11_out_2));
  _16bitshift u_16bitshift_12 (.in_1(n16bitshift_11_out_2), .out_2(n16bitshift_12_out_2));
  _16bitshift u_16bitshift_13 (.in_1(n16bitshift_12_out_2), .out_2(n16bitshift_13_out_2));
  _16bitshift u_16bitshift_14 (.in_1(n16bitshift_13_out_2), .out_2(n16bitshift_14_out_2));
  _16bitshift u_16bitshift_15 (.in_1(n16bitshift_14_out_2), .out_2(n16bitshift_15_out_2));
  Adder #(.width(16)) adder_6 (.a(n16bitshift_15_out_2), .b(adder_5_out), .out(adder_6_out));  // open: cin, cout
  multhelper multhelper_7 (.in_1({{8{1'b0}}, and_9_out}), .out_3(multhelper_7_out_3), .in_2(and_7_out));
  _16bitshift u_16bitshift_16 (.in_1(multhelper_7_out_3), .out_2(n16bitshift_16_out_2));
  _16bitshift u_16bitshift_17 (.in_1(n16bitshift_16_out_2), .out_2(n16bitshift_17_out_2));
  _16bitshift u_16bitshift_18 (.in_1(n16bitshift_17_out_2), .out_2(n16bitshift_18_out_2));
  _16bitshift u_16bitshift_19 (.in_1(n16bitshift_18_out_2), .out_2(n16bitshift_19_out_2));
  _16bitshift u_16bitshift_20 (.in_1(n16bitshift_19_out_2), .out_2(n16bitshift_20_out_2));
  _16bitshift u_16bitshift_21 (.in_1(n16bitshift_20_out_2), .out_2(n16bitshift_21_out_2));
  Adder #(.width(16)) adder_7 (.a(n16bitshift_21_out_2), .b(adder_6_out), .out(adder_7_out));  // open: cin, cout
  multhelper multhelper_8 (.in_1({{8{1'b0}}, and_9_out}), .out_3(multhelper_8_out_3), .in_2(and_8_out));
  _16bitshift u_16bitshift_22 (.in_1(multhelper_8_out_3), .out_2(n16bitshift_22_out_2));
  _16bitshift u_16bitshift_23 (.in_1(n16bitshift_22_out_2), .out_2(n16bitshift_23_out_2));
  _16bitshift u_16bitshift_24 (.in_1(n16bitshift_23_out_2), .out_2(n16bitshift_24_out_2));
  _16bitshift u_16bitshift_25 (.in_1(n16bitshift_24_out_2), .out_2(n16bitshift_25_out_2));
  _16bitshift u_16bitshift_26 (.in_1(n16bitshift_25_out_2), .out_2(n16bitshift_26_out_2));
  _16bitshift u_16bitshift_27 (.in_1(n16bitshift_26_out_2), .out_2(n16bitshift_27_out_2));
  _16bitshift u_16bitshift_28 (.in_1(n16bitshift_27_out_2), .out_2(n16bitshift_28_out_2));
  Adder #(.width(16)) adder_8 (.a(n16bitshift_28_out_2), .b(adder_7_out), .out(adder_8_out));  // open: cin, cout
  not not_1 (not_1_out, Overflow);
  and and_33 (Negative, not_1_out, out_9[7]);
  or or_2 (Overflow, or_3_out, xor_1_out);
  or or_3 (or_3_out, adder_8_out[8], adder_8_out[9], adder_8_out[10], adder_8_out[11], adder_8_out[12], adder_8_out[13], adder_8_out[14], adder_8_out[15]);
  or or_4 (out_9[0], half_adder_1_out_3, adder_8_out[0]);
  or or_5 (out_9[1], full_adder_1_out_4, adder_8_out[1]);
  or or_6 (out_9[2], full_adder_2_out_4, adder_8_out[2]);
  or or_7 (out_9[3], full_adder_3_out_4, adder_8_out[3]);
  or or_8 (out_9[4], full_adder_4_out_4, adder_8_out[4]);
  or or_9 (out_9[5], full_adder_5_out_4, adder_8_out[5]);
  or or_10 (out_9[6], full_adder_6_out_4, adder_8_out[6]);
  or or_11 (out_9[7], full_adder_7_out_4, adder_8_out[7]);
  not not_2 (not_2_out, out_9[1]);
  not not_3 (not_3_out, out_9[0]);
  not not_4 (not_4_out, out_9[2]);
  not not_5 (not_5_out, out_9[6]);
  not not_6 (not_6_out, out_9[3]);
  not not_7 (not_7_out, out_9[4]);
  not not_8 (not_8_out, out_9[5]);
  not not_9 (not_9_out, out_9[7]);
  and and_34 (Zero, not_3_out, not_2_out, not_4_out, not_6_out, not_7_out, not_8_out, not_5_out, not_9_out);

  // Notes on the sheet:
  //   R
  //   L
  //   SUB Section OPCODE required
  //   MULT SECTION OPCODE
  //   1 = SUB ON 0 = SUB OFF
  //   1= MULT ON 0= MULT OFF
  //   ADD Section OPCODE required
  //   1 = ADD ON 0 = ADD OFF
  //   Multiplication has no signed overflow check. Beware when using it with signed integers.
  //   If there is an overflow, we can't tell the sign.
endmodule

module full_adder (
  input  in_1,
  input  in_2,
  input  in_3,
  output out_4,
  output out_5
);

  wire and_1_out, and_2_out, xor_1_out;

  xor xor_1 (xor_1_out, in_2, in_3);
  and and_1 (and_1_out, in_1, xor_1_out);
  or or_1 (out_5, and_1_out, and_2_out);
  and and_2 (and_2_out, in_2, in_3);
  xor xor_2 (out_4, in_1, xor_1_out);
endmodule

module half_adder (
  input  in_1,
  input  in_2,
  output out_3,
  output out_4
);

  xor xor_1 (out_3, in_1, in_2);
  and and_1 (out_4, in_1, in_2);
endmodule

module ALU2C (
  input  in_1,
  input  [7:0] in_2,
  output [7:0] out_3
);

  wire and_1_out, and_2_out, and_3_out, and_4_out, and_5_out, and_6_out, and_7_out, and_8_out, and_9_out,
       and_10_out, and_11_out, and_12_out, and_13_out, and_14_out, and_15_out, and_16_out,
       full_adder_1_out_5, full_adder_2_out_5, full_adder_3_out_5, full_adder_4_out_5, full_adder_5_out_5,
       full_adder_6_out_5, half_adder_1_out_4, not_1_out, not_2_out, not_3_out, not_4_out, not_5_out,
       not_6_out, not_7_out, not_8_out, not_9_out, not_10_out, not_11_out, not_12_out, not_13_out,
       not_14_out, not_15_out, not_16_out, or_1_out, or_2_out, or_3_out, or_4_out, or_5_out, or_6_out,
       or_7_out, or_8_out;

  not not_1 (not_1_out, in_1);
  not not_2 (not_2_out, in_2[0]);
  not not_3 (not_3_out, in_1);
  not not_4 (not_4_out, in_2[1]);
  not not_5 (not_5_out, in_1);
  not not_6 (not_6_out, in_2[2]);
  not not_7 (not_7_out, in_1);
  not not_8 (not_8_out, in_2[3]);
  not not_9 (not_9_out, in_1);
  not not_10 (not_10_out, in_2[4]);
  not not_11 (not_11_out, in_1);
  not not_12 (not_12_out, in_2[5]);
  not not_13 (not_13_out, in_1);
  not not_14 (not_14_out, in_2[6]);
  not not_15 (not_15_out, in_1);
  not not_16 (not_16_out, in_2[7]);
  and and_1 (and_1_out, not_1_out, in_2[0]);
  or or_1 (or_1_out, and_1_out, and_2_out);
  and and_2 (and_2_out, in_1, not_2_out);
  and and_3 (and_3_out, not_3_out, in_2[1]);
  or or_2 (or_2_out, and_3_out, and_4_out);
  and and_4 (and_4_out, in_1, not_4_out);
  and and_5 (and_5_out, not_5_out, in_2[2]);
  or or_3 (or_3_out, and_5_out, and_6_out);
  and and_6 (and_6_out, in_1, not_6_out);
  and and_7 (and_7_out, not_7_out, in_2[3]);
  or or_4 (or_4_out, and_7_out, and_8_out);
  and and_8 (and_8_out, in_1, not_8_out);
  and and_9 (and_9_out, not_9_out, in_2[4]);
  or or_5 (or_5_out, and_9_out, and_10_out);
  and and_10 (and_10_out, in_1, not_10_out);
  and and_11 (and_11_out, not_11_out, in_2[5]);
  or or_6 (or_6_out, and_11_out, and_12_out);
  and and_12 (and_12_out, in_1, not_12_out);
  and and_13 (and_13_out, not_13_out, in_2[6]);
  or or_7 (or_7_out, and_13_out, and_14_out);
  and and_14 (and_14_out, in_1, not_14_out);
  and and_15 (and_15_out, not_15_out, in_2[7]);
  or or_8 (or_8_out, and_15_out, and_16_out);
  and and_16 (and_16_out, in_1, not_16_out);
  half_adder half_adder_1 (.in_1(or_1_out), .in_2(in_1), .out_3(out_3[0]), .out_4(half_adder_1_out_4));
  full_adder full_adder_1 (
    .in_2(or_2_out), .in_3(1'b0), .out_4(out_3[1]), .in_1(half_adder_1_out_4), .out_5(full_adder_1_out_5));
  full_adder full_adder_2 (
    .in_2(or_3_out), .in_3(1'b0), .out_4(out_3[2]), .in_1(full_adder_1_out_5), .out_5(full_adder_2_out_5));
  full_adder full_adder_3 (
    .in_2(or_4_out), .in_3(1'b0), .out_4(out_3[3]), .in_1(full_adder_2_out_5), .out_5(full_adder_3_out_5));
  full_adder full_adder_4 (
    .in_2(or_5_out), .in_3(1'b0), .out_4(out_3[4]), .in_1(full_adder_3_out_5), .out_5(full_adder_4_out_5));
  full_adder full_adder_5 (
    .in_2(or_6_out), .in_3(1'b0), .out_4(out_3[5]), .in_1(full_adder_4_out_5), .out_5(full_adder_5_out_5));
  full_adder full_adder_6 (
    .in_2(or_7_out), .in_3(1'b0), .out_4(out_3[6]), .in_1(full_adder_5_out_5), .out_5(full_adder_6_out_5));
  full_adder full_adder_7 (.in_2(or_8_out), .in_3(1'b0), .out_4(out_3[7]), .in_1(full_adder_6_out_5));  // open: out_5
endmodule

module _16bitshift (
  input  [15:0] in_1,
  output [15:0] out_2
);


  assign out_2 = {in_1[14:0], 1'b0};
endmodule

module multhelper (
  input  [15:0] in_1,
  input  in_2,
  output [15:0] out_3
);

  and and_1 (out_3[0], in_1[0], in_2);
  and and_2 (out_3[1], in_1[1], in_2);
  and and_3 (out_3[2], in_1[2], in_2);
  and and_4 (out_3[3], in_1[3], in_2);
  and and_5 (out_3[4], in_1[4], in_2);
  and and_6 (out_3[5], in_1[5], in_2);
  and and_7 (out_3[6], in_1[6], in_2);
  and and_8 (out_3[7], in_1[7], in_2);
  and and_9 (out_3[8], in_1[8], in_2);
  and and_10 (out_3[9], in_1[9], in_2);
  and and_11 (out_3[10], in_1[10], in_2);
  and and_12 (out_3[11], in_1[11], in_2);
  and and_13 (out_3[12], in_1[12], in_2);
  and and_14 (out_3[13], in_1[13], in_2);
  and and_15 (out_3[14], in_1[14], in_2);
  and and_16 (out_3[15], in_1[15], in_2);
endmodule

module StatusRegister (
  input  CLK,
  input  R_W,
  input  ENABLE,
  input  [2:0] INPUT,
  output [2:0] out_5
);

  wire and_1_out, and_2_out, and_3_out, and_4_out, and_5_out, not_1_out, not_2_out, not_3_out, not_4_out,
       s_r_ff_1_q, s_r_ff_2_q, s_r_ff_3_q;

  and and_1 (and_1_out, CLK, ENABLE);
  and and_2 (and_2_out, CLK, R_W, ENABLE);
  and and_3 (and_3_out, INPUT[0], CLK, R_W);
  not not_1 (not_1_out, and_3_out);
  and and_4 (and_4_out, INPUT[1], CLK, R_W);
  not not_2 (not_2_out, and_4_out);
  and and_5 (and_5_out, INPUT[2], CLK, R_W);
  not not_3 (not_3_out, and_5_out);
  not not_4 (not_4_out, R_W);
  S_R_Flip_Flop #(.trigger("high")) s_r_ff_1 (
    .S(and_3_out), .clk(and_2_out), .R(not_1_out), .Q(s_r_ff_1_q));  // open: Qn, preset, reset, en
  S_R_Flip_Flop #(.trigger("high")) s_r_ff_2 (
    .S(and_4_out), .clk(and_2_out), .R(not_2_out), .Q(s_r_ff_2_q));  // open: Qn, preset, reset, en
  S_R_Flip_Flop #(.trigger("high")) s_r_ff_3 (
    .S(and_5_out), .clk(and_2_out), .R(not_3_out), .Q(s_r_ff_3_q));  // open: Qn, preset, reset, en
  and and_6 (out_5[0], s_r_ff_1_q, and_1_out, not_4_out);
  and and_7 (out_5[1], s_r_ff_2_q, and_1_out, not_4_out);
  and and_8 (out_5[2], s_r_ff_3_q, and_1_out, not_4_out);
endmodule

module _3_Combinator (
  input  in_1,
  input  [7:0] in_2,
  input  in_3,
  input  [7:0] in_4,
  input  in_5,
  input  [7:0] in_6,
  output [7:0] out_7
);

  wire and_1_out, and_2_out, and_3_out, and_4_out, and_5_out, and_6_out, and_7_out, and_8_out, and_9_out,
       and_10_out, and_11_out, and_12_out, and_13_out, and_14_out, and_15_out, and_16_out, and_17_out,
       and_18_out, and_19_out, and_20_out, and_21_out, and_22_out, and_23_out, and_24_out;

  and and_1 (and_1_out, in_2[0], in_1);
  and and_2 (and_2_out, in_2[1], in_1);
  and and_3 (and_3_out, in_2[2], in_1);
  and and_4 (and_4_out, in_2[3], in_1);
  and and_5 (and_5_out, in_2[4], in_1);
  and and_6 (and_6_out, in_2[5], in_1);
  and and_7 (and_7_out, in_2[6], in_1);
  and and_8 (and_8_out, in_2[7], in_1);
  and and_9 (and_9_out, in_4[0], in_3);
  and and_10 (and_10_out, in_4[1], in_3);
  and and_11 (and_11_out, in_4[2], in_3);
  and and_12 (and_12_out, in_4[3], in_3);
  and and_13 (and_13_out, in_4[4], in_3);
  and and_14 (and_14_out, in_4[5], in_3);
  and and_15 (and_15_out, in_4[6], in_3);
  and and_16 (and_16_out, in_4[7], in_3);
  and and_17 (and_17_out, in_6[0], in_5);
  and and_18 (and_18_out, in_6[1], in_5);
  and and_19 (and_19_out, in_6[2], in_5);
  and and_20 (and_20_out, in_6[3], in_5);
  and and_21 (and_21_out, in_6[4], in_5);
  and and_22 (and_22_out, in_6[5], in_5);
  and and_23 (and_23_out, in_6[6], in_5);
  and and_24 (and_24_out, in_6[7], in_5);
  or or_1 (out_7[0], and_1_out, and_9_out, and_17_out);
  or or_2 (out_7[1], and_2_out, and_10_out, and_18_out);
  or or_3 (out_7[2], and_3_out, and_11_out, and_19_out);
  or or_4 (out_7[3], and_4_out, and_12_out, and_20_out);
  or or_5 (out_7[4], and_5_out, and_13_out, and_21_out);
  or or_6 (out_7[5], and_6_out, and_14_out, and_22_out);
  or or_7 (out_7[6], and_7_out, and_15_out, and_23_out);
  or or_8 (out_7[7], and_8_out, and_16_out, and_24_out);
endmodule

module _4_combinator (
  input  in_1,
  input  [7:0] in_2,
  input  in_3,
  input  [7:0] in_4,
  input  in_5,
  input  [7:0] in_6,
  input  in_7,
  input  [7:0] in_8,
  output [7:0] out_9
);

  wire and_1_out, and_2_out, and_3_out, and_4_out, and_5_out, and_6_out, and_7_out, and_8_out, and_9_out,
       and_10_out, and_11_out, and_12_out, and_13_out, and_14_out, and_15_out, and_16_out, and_17_out,
       and_18_out, and_19_out, and_20_out, and_21_out, and_22_out, and_23_out, and_24_out, and_25_out,
       and_26_out, and_27_out, and_28_out, and_29_out, and_30_out, and_31_out, and_32_out;

  and and_1 (and_1_out, in_2[0], in_1);
  and and_2 (and_2_out, in_2[1], in_1);
  and and_3 (and_3_out, in_2[2], in_1);
  and and_4 (and_4_out, in_2[3], in_1);
  and and_5 (and_5_out, in_2[4], in_1);
  and and_6 (and_6_out, in_2[5], in_1);
  and and_7 (and_7_out, in_2[6], in_1);
  and and_8 (and_8_out, in_2[7], in_1);
  and and_9 (and_9_out, in_4[0], in_3);
  and and_10 (and_10_out, in_4[1], in_3);
  and and_11 (and_11_out, in_4[2], in_3);
  and and_12 (and_12_out, in_4[3], in_3);
  and and_13 (and_13_out, in_4[4], in_3);
  and and_14 (and_14_out, in_4[5], in_3);
  and and_15 (and_15_out, in_4[6], in_3);
  and and_16 (and_16_out, in_4[7], in_3);
  and and_17 (and_17_out, in_6[0], in_5);
  and and_18 (and_18_out, in_6[1], in_5);
  and and_19 (and_19_out, in_6[2], in_5);
  and and_20 (and_20_out, in_6[3], in_5);
  and and_21 (and_21_out, in_6[4], in_5);
  and and_22 (and_22_out, in_6[5], in_5);
  and and_23 (and_23_out, in_6[6], in_5);
  and and_24 (and_24_out, in_6[7], in_5);
  and and_25 (and_25_out, in_8[0], in_7);
  and and_26 (and_26_out, in_8[1], in_7);
  and and_27 (and_27_out, in_8[2], in_7);
  and and_28 (and_28_out, in_8[3], in_7);
  and and_29 (and_29_out, in_8[4], in_7);
  and and_30 (and_30_out, in_8[5], in_7);
  and and_31 (and_31_out, in_8[6], in_7);
  and and_32 (and_32_out, in_8[7], in_7);
  or or_1 (out_9[0], and_1_out, and_9_out, and_17_out, and_25_out);
  or or_2 (out_9[1], and_2_out, and_10_out, and_18_out, and_26_out);
  or or_3 (out_9[2], and_3_out, and_11_out, and_19_out, and_27_out);
  or or_4 (out_9[3], and_4_out, and_12_out, and_20_out, and_28_out);
  or or_5 (out_9[4], and_5_out, and_13_out, and_21_out, and_29_out);
  or or_6 (out_9[5], and_6_out, and_14_out, and_22_out, and_30_out);
  or or_7 (out_9[6], and_7_out, and_15_out, and_23_out, and_31_out);
  or or_8 (out_9[7], and_8_out, and_16_out, and_24_out, and_32_out);
endmodule

module _5_combinator (
  input  in_1,
  input  [7:0] in_2,
  input  in_3,
  input  [7:0] in_4,
  input  in_5,
  input  [7:0] in_6,
  input  in_7,
  input  [7:0] in_8,
  input  in_9,
  input  [7:0] in_10,
  output [7:0] out_11
);

  wire and_1_out, and_2_out, and_3_out, and_4_out, and_5_out, and_6_out, and_7_out, and_8_out, and_9_out,
       and_10_out, and_11_out, and_12_out, and_13_out, and_14_out, and_15_out, and_16_out, and_17_out,
       and_18_out, and_19_out, and_20_out, and_21_out, and_22_out, and_23_out, and_24_out, and_25_out,
       and_26_out, and_27_out, and_28_out, and_29_out, and_30_out, and_31_out, and_32_out, and_33_out,
       and_34_out, and_35_out, and_36_out, and_37_out, and_38_out, and_39_out, and_40_out;
  wire [7:0] or_1_out, or_9_out;

  and and_1 (and_1_out, in_2[0], in_1);
  and and_2 (and_2_out, in_2[1], in_1);
  and and_3 (and_3_out, in_2[2], in_1);
  and and_4 (and_4_out, in_2[3], in_1);
  and and_5 (and_5_out, in_2[4], in_1);
  and and_6 (and_6_out, in_2[5], in_1);
  and and_7 (and_7_out, in_2[6], in_1);
  and and_8 (and_8_out, in_2[7], in_1);
  and and_9 (and_9_out, in_4[0], in_3);
  and and_10 (and_10_out, in_4[1], in_3);
  and and_11 (and_11_out, in_4[2], in_3);
  and and_12 (and_12_out, in_4[3], in_3);
  and and_13 (and_13_out, in_4[4], in_3);
  and and_14 (and_14_out, in_4[5], in_3);
  and and_15 (and_15_out, in_4[6], in_3);
  and and_16 (and_16_out, in_4[7], in_3);
  and and_17 (and_17_out, in_6[0], in_5);
  and and_18 (and_18_out, in_6[1], in_5);
  and and_19 (and_19_out, in_6[2], in_5);
  and and_20 (and_20_out, in_6[3], in_5);
  and and_21 (and_21_out, in_6[4], in_5);
  and and_22 (and_22_out, in_6[5], in_5);
  and and_23 (and_23_out, in_6[6], in_5);
  and and_24 (and_24_out, in_6[7], in_5);
  and and_25 (and_25_out, in_8[0], in_7);
  and and_26 (and_26_out, in_8[1], in_7);
  and and_27 (and_27_out, in_8[2], in_7);
  and and_28 (and_28_out, in_8[3], in_7);
  and and_29 (and_29_out, in_8[4], in_7);
  and and_30 (and_30_out, in_8[5], in_7);
  and and_31 (and_31_out, in_8[6], in_7);
  and and_32 (and_32_out, in_8[7], in_7);
  and and_33 (and_33_out, in_10[0], in_9);
  and and_34 (and_34_out, in_10[1], in_9);
  and and_35 (and_35_out, in_10[2], in_9);
  and and_36 (and_36_out, in_10[3], in_9);
  and and_37 (and_37_out, in_10[4], in_9);
  and and_38 (and_38_out, in_10[5], in_9);
  and and_39 (and_39_out, in_10[6], in_9);
  and and_40 (and_40_out, in_10[7], in_9);
  or or_1 (or_1_out[0], and_1_out, and_9_out, and_17_out);
  or or_2 (or_1_out[1], and_2_out, and_10_out, and_18_out);
  or or_3 (or_1_out[2], and_3_out, and_11_out, and_19_out);
  or or_4 (or_1_out[3], and_4_out, and_12_out, and_20_out);
  or or_5 (or_1_out[4], and_5_out, and_13_out, and_21_out);
  or or_6 (or_1_out[5], and_6_out, and_14_out, and_22_out);
  or or_7 (or_1_out[6], and_7_out, and_15_out, and_23_out);
  or or_8 (or_1_out[7], and_8_out, and_16_out, and_24_out);
  or or_9 (or_9_out[0], and_25_out, and_33_out);
  or or_10 (or_9_out[1], and_26_out, and_34_out);
  or or_11 (or_9_out[2], and_27_out, and_35_out);
  or or_12 (or_9_out[3], and_28_out, and_36_out);
  or or_13 (or_9_out[4], and_29_out, and_37_out);
  or or_14 (or_9_out[5], and_30_out, and_38_out);
  or or_15 (or_9_out[6], and_31_out, and_39_out);
  or or_16 (or_9_out[7], and_32_out, and_40_out);
  assign out_11 = or_1_out | or_9_out;  // OR_Gate or_17, 8 bits wide
endmodule

module _2_Combinator (
  input  in_1,
  input  [7:0] in_2,
  input  in_3,
  input  [7:0] in_4,
  output [7:0] out_5
);

  wire and_1_out, and_2_out, and_3_out, and_4_out, and_5_out, and_6_out, and_7_out, and_8_out, and_9_out,
       and_10_out, and_11_out, and_12_out, and_13_out, and_14_out, and_15_out, and_16_out, undriven;

  and and_1 (and_1_out, in_2[0], in_1);
  and and_2 (and_2_out, in_2[1], in_1);
  and and_3 (and_3_out, in_2[2], in_1);
  and and_4 (and_4_out, in_2[3], in_1);
  and and_5 (and_5_out, in_2[4], in_1);
  and and_6 (and_6_out, in_2[5], in_1);
  and and_7 (and_7_out, in_2[6], in_1);
  and and_8 (and_8_out, in_2[7], in_1);
  and and_9 (and_9_out, in_4[0], in_3);
  and and_10 (and_10_out, in_4[1], in_3);
  and and_11 (and_11_out, in_4[2], in_3);
  and and_12 (and_12_out, in_4[3], in_3);
  and and_13 (and_13_out, in_4[4], in_3);
  and and_14 (and_14_out, in_4[5], in_3);
  and and_15 (and_15_out, in_4[6], in_3);
  and and_16 (and_16_out, in_4[7], in_3);
  // AND_Gate and_17 has open pins: in1=undriven, out=open
  or or_1 (out_5[0], and_1_out, and_9_out);
  or or_2 (out_5[1], and_2_out, and_10_out);
  or or_3 (out_5[2], and_3_out, and_11_out);
  or or_4 (out_5[3], and_4_out, and_12_out);
  or or_5 (out_5[4], and_5_out, and_13_out);
  or or_6 (out_5[5], and_6_out, and_14_out);
  or or_7 (out_5[6], and_7_out, and_15_out);
  or or_8 (out_5[7], and_8_out, and_16_out);
endmodule

module Incrementer (
  input  [7:0] in_1,
  output [7:0] out_2
);

  wire full_adder_1_out_5, full_adder_2_out_5, half_adder_1_out_4;

  half_adder half_adder_1 (.in_1(in_1[0]), .in_2(1'b1), .out_3(out_2[0]), .out_4(half_adder_1_out_4));
  full_adder full_adder_1 (
    .in_2(in_1[1]), .in_3(1'b0), .out_4(out_2[1]), .in_1(half_adder_1_out_4), .out_5(full_adder_1_out_5));
  full_adder full_adder_2 (
    .in_2(in_1[2]), .in_3(1'b0), .out_4(out_2[2]), .in_1(full_adder_1_out_5), .out_5(full_adder_2_out_5));
  full_adder full_adder_3 (.in_2(in_1[3]), .in_3(1'b0), .out_4(out_2[3]), .in_1(full_adder_2_out_5));  // open: out_5

  assign out_2[7:4] = 4'b0000;
endmodule

module PCregister (
  input  CLK,
  input  R_W,
  input  ENABLE,
  input  [7:0] in_4,
  input  [2:0] in_5,
  input  in_6,
  output [7:0] out_7
);

  wire and_1_out, and_2_out, and_3_out, and_4_out, and_5_out, and_6_out, multiplexer_1_out,
       multiplexer_2_out, multiplexer_3_out, not_1_out, not_2_out, not_3_out, not_4_out, not_5_out,
       s_r_ff_1_q, s_r_ff_2_q, s_r_ff_3_q, s_r_ff_4_q;

  Multiplexer #(.disabled(0), .enable("false")) multiplexer_1 (
    .in0(in_4[0]), .in1(in_5[0]), .out(multiplexer_1_out), .sel(in_6));
  Multiplexer #(.disabled(0), .enable("false")) multiplexer_2 (
    .in0(in_4[1]), .in1(in_5[1]), .out(multiplexer_2_out), .sel(in_6));
  Multiplexer #(.disabled(0), .enable("false")) multiplexer_3 (
    .in0(in_4[2]), .in1(in_5[2]), .out(multiplexer_3_out), .sel(in_6));
  and and_1 (and_1_out, CLK, ENABLE);
  and and_2 (and_2_out, CLK, ENABLE);
  and and_3 (and_3_out, multiplexer_1_out, CLK, R_W);
  and and_4 (and_4_out, multiplexer_2_out, CLK, R_W);
  and and_5 (and_5_out, multiplexer_3_out, CLK, R_W);
  and and_6 (and_6_out, in_4[3], CLK, R_W);
  not not_1 (not_1_out, R_W);
  S_R_Flip_Flop #(.trigger("high")) s_r_ff_1 (
    .S(and_3_out), .clk(and_2_out), .R(not_2_out), .Q(s_r_ff_1_q));  // open: Qn, preset, reset, en
  not not_2 (not_2_out, and_3_out);
  S_R_Flip_Flop #(.trigger("high")) s_r_ff_2 (
    .S(and_4_out), .clk(and_2_out), .R(not_3_out), .Q(s_r_ff_2_q));  // open: Qn, preset, reset, en
  not not_3 (not_3_out, and_4_out);
  S_R_Flip_Flop #(.trigger("high")) s_r_ff_3 (
    .S(and_5_out), .clk(and_2_out), .R(not_4_out), .Q(s_r_ff_3_q));  // open: Qn, preset, reset, en
  not not_4 (not_4_out, and_5_out);
  S_R_Flip_Flop #(.trigger("high")) s_r_ff_4 (
    .S(and_6_out), .clk(and_2_out), .R(not_5_out), .Q(s_r_ff_4_q));  // open: Qn, preset, reset, en
  not not_5 (not_5_out, and_6_out);
  and and_7 (out_7[0], s_r_ff_1_q, and_1_out, not_1_out);
  and and_8 (out_7[1], s_r_ff_2_q, and_1_out, not_1_out);
  and and_9 (out_7[2], s_r_ff_3_q, and_1_out, not_1_out);
  and and_10 (out_7[3], s_r_ff_4_q, and_1_out, not_1_out);

  assign out_7[7:4] = 4'b0000;

  // Notes on the sheet:
  //   INPUT
endmodule
